// Logisim project matrix de led.circ as structural Verilog: 8 circuits, main circuit main
module main (
  input  [3:0] in_1
);

  wire [6:0] mux_matrix_led_1_out_2, mux_matrix_led_1_out_3, mux_matrix_led_1_out_4, mux_matrix_led_1_out_5,
       mux_matrix_led_1_out_6;
  wire [7:0] numero_to_ascii_1_out_2;

  MUX_MATRIX_LED mux_matrix_led_1 (
    .in_1(numero_to_ascii_1_out_2), .out_2(mux_matrix_led_1_out_2), .out_3(mux_matrix_led_1_out_3),
    .out_4(mux_matrix_led_1_out_4), .out_5(mux_matrix_led_1_out_5), .out_6(mux_matrix_led_1_out_6));
  NUMERO_TO_ASCII numero_to_ascii_1 (.in_1(in_1), .out_2(numero_to_ascii_1_out_2));
  DotMatrix dotmatrix_1 (
    .col0(mux_matrix_led_1_out_2), .col1(mux_matrix_led_1_out_3), .col2(mux_matrix_led_1_out_4),
    .col3(mux_matrix_led_1_out_5), .col4(mux_matrix_led_1_out_6));
endmodule

module MUX_MATRIX_LED (
  input  [7:0] in_1,
  output [6:0] out_2,
  output [6:0] out_3,
  output [6:0] out_4,
  output [6:0] out_5,
  output [6:0] out_6
);

  COLUNA_0 coluna_0_1 (
    .a0(in_1[7]), .a1(in_1[6]), .a2(in_1[5]), .a3(in_1[4]), .a4(in_1[3]), .a5(in_1[2]), .a6(in_1[1]),
    .a7(in_1[0]), .x00(out_2[6]), .x10(out_2[5]), .x20(out_2[4]), .x30(out_2[3]), .x40(out_2[2]),
    .x50(out_2[1]), .x60(out_2[0]));
  COLUNA_1 coluna_1_1 (
    .a0(in_1[7]), .a1(in_1[6]), .a2(in_1[5]), .a3(in_1[4]), .a4(in_1[3]), .a5(in_1[2]), .a6(in_1[1]),
    .a7(in_1[0]), .x00(out_3[6]), .x10(out_3[5]), .x20(out_3[4]), .x30(out_3[3]), .x40(out_3[2]),
    .x50(out_3[1]), .x60(out_3[0]));
  COLUNA_2 coluna_2_1 (
    .a0(in_1[7]), .a1(in_1[6]), .a2(in_1[5]), .a3(in_1[4]), .a4(in_1[3]), .a5(in_1[2]), .a6(in_1[1]),
    .a7(in_1[0]), .x00(out_4[6]), .x10(out_4[5]), .x20(out_4[4]), .x30(out_4[3]), .x40(out_4[2]),
    .x50(out_4[1]), .x60(out_4[0]));
  COLUNA_3 coluna_3_1 (
    .a0(in_1[7]), .a1(in_1[6]), .a2(in_1[5]), .a3(in_1[4]), .a4(in_1[3]), .a5(in_1[2]), .a6(in_1[1]),
    .a7(in_1[0]), .x00(out_5[6]), .x10(out_5[5]), .x20(out_5[4]), .x30(out_5[3]), .x40(out_5[2]),
    .x50(out_5[1]), .x60(out_5[0]));
  COLUNA_4 coluna_4_1 (
    .a0(in_1[7]), .a1(in_1[6]), .a2(in_1[5]), .a3(in_1[4]), .a4(in_1[3]), .a5(in_1[2]), .a6(in_1[1]),
    .a7(in_1[0]), .x00(out_6[6]), .x10(out_6[5]), .x20(out_6[4]), .x30(out_6[3]), .x40(out_6[2]),
    .x50(out_6[1]), .x60(out_6[0]));
endmodule

module COLUNA_0 (
  input  a0,
  input  a1,
  input  a2,
  input  a3,
  input  a4,
  input  a5,
  input  a6,
  input  a7,
  output x00,
  output x10,
  output x20,
  output x30,
  output x40,
  output x50,
  output x60
);

  wire and_1_out, and_2_out, and_3_out, and_4_out, and_5_out, and_6_out, and_7_out, and_8_out, and_9_out,
       and_10_out, and_11_out, and_12_out, and_13_out, and_14_out, and_15_out, and_16_out, and_17_out,
       and_18_out, and_19_out, and_20_out, and_21_out, and_22_out, and_23_out, and_24_out, and_25_out,
       and_26_out, and_27_out, and_28_out, and_29_out, and_30_out, and_31_out, and_32_out, and_33_out,
       and_34_out, and_35_out, and_36_out, and_37_out, and_38_out, and_39_out, and_40_out, and_41_out,
       and_42_out, and_43_out, and_44_out, and_45_out, and_46_out, and_47_out, and_48_out, and_49_out,
       and_50_out, and_51_out, and_52_out, and_53_out, and_54_out, and_55_out, and_56_out, and_57_out,
       and_58_out, and_59_out, and_60_out, and_61_out, and_62_out, and_63_out, and_64_out, not_1_out,
       not_2_out, not_3_out, not_4_out, not_5_out, not_6_out, not_7_out, not_8_out, not_9_out, not_10_out,
       not_11_out, not_12_out, not_13_out, not_14_out, not_15_out, not_16_out, not_17_out, not_18_out,
       not_19_out, not_20_out, not_21_out, not_22_out, not_23_out, not_24_out, not_25_out, not_26_out,
       not_27_out, not_28_out, not_29_out, not_30_out, not_31_out, not_32_out, not_33_out, not_34_out,
       not_35_out, not_36_out, not_37_out, not_38_out, not_39_out, not_40_out, not_41_out, not_42_out,
       not_43_out, not_44_out, not_45_out, not_46_out, not_47_out, not_48_out, not_49_out, not_50_out,
       not_51_out, not_52_out, not_53_out, not_54_out, not_55_out, not_56_out, not_57_out, not_58_out,
       not_59_out, not_60_out, not_61_out, not_62_out, not_63_out, not_64_out, not_65_out, not_66_out,
       not_67_out, not_68_out, not_69_out, not_70_out, not_71_out, not_72_out, not_73_out, not_74_out,
       not_75_out, not_76_out, not_77_out, not_78_out, not_79_out, not_80_out, not_81_out, not_82_out,
       not_83_out, not_84_out, not_85_out, not_86_out, not_87_out, not_88_out, not_89_out, not_90_out,
       not_91_out, not_92_out, not_93_out, not_94_out, not_95_out, not_96_out, not_97_out, not_98_out,
       not_99_out, not_100_out, not_101_out, not_102_out, not_103_out, not_104_out, not_105_out, not_106_out,
       not_107_out, not_108_out, not_109_out, not_110_out, not_111_out, not_112_out, not_113_out,
       not_114_out, not_115_out, not_116_out, not_117_out, not_118_out, not_119_out, not_120_out,
       not_121_out, not_122_out, not_123_out, not_124_out, not_125_out, not_126_out, not_127_out,
       not_128_out, not_129_out, not_130_out, not_131_out, not_132_out, not_133_out, not_134_out,
       not_135_out, not_136_out, not_137_out, not_138_out, not_139_out, not_140_out, not_141_out,
       not_142_out, not_143_out, not_144_out, not_145_out, not_146_out, not_147_out, not_148_out,
       not_149_out, not_150_out, not_151_out, not_152_out, not_153_out, not_154_out, not_155_out,
       not_156_out, not_157_out, not_158_out, not_159_out, not_160_out, not_161_out, not_162_out,
       not_163_out, not_164_out, not_165_out, not_166_out, not_167_out, not_168_out, not_169_out,
       not_170_out, not_171_out, not_172_out, not_173_out, not_174_out, not_175_out, not_176_out,
       not_177_out, not_178_out, not_179_out, not_180_out, not_181_out, not_182_out, not_183_out,
       not_184_out, not_185_out, not_186_out, not_187_out, not_188_out, not_189_out, not_190_out,
       not_191_out, not_192_out, not_193_out, not_194_out, not_195_out, not_196_out, not_197_out,
       not_198_out, not_199_out, not_200_out, not_201_out, not_202_out, not_203_out, not_204_out,
       not_205_out, not_206_out, not_207_out, not_208_out, not_209_out, not_210_out, not_211_out,
       not_212_out, not_213_out, not_214_out, not_215_out, not_216_out, not_217_out, not_218_out,
       not_219_out, not_220_out, not_221_out, not_222_out, not_223_out, not_224_out, not_225_out,
       not_226_out, not_227_out, not_228_out, not_229_out, not_230_out, not_231_out, not_232_out,
       not_233_out, not_234_out, not_235_out, not_236_out, not_237_out, not_238_out, not_239_out,
       not_240_out, not_241_out, not_242_out, not_243_out, not_244_out, not_245_out, not_246_out;

  not not_1 (not_1_out, a0);
  not not_2 (not_2_out, a1);
  not not_3 (not_3_out, a4);
  not not_4 (not_4_out, a0);
  not not_5 (not_5_out, a2);
  not not_6 (not_6_out, a4);
  not not_7 (not_7_out, a7);
  not not_8 (not_8_out, a0);
  not not_9 (not_9_out, a2);
  not not_10 (not_10_out, a3);
  not not_11 (not_11_out, a6);
  not not_12 (not_12_out, a0);
  not not_13 (not_13_out, a2);
  not not_14 (not_14_out, a3);
  not not_15 (not_15_out, a7);
  not not_16 (not_16_out, a0);
  not not_17 (not_17_out, a2);
  not not_18 (not_18_out, a5);
  not not_19 (not_19_out, a6);
  not not_20 (not_20_out, a0);
  not not_21 (not_21_out, a2);
  not not_22 (not_22_out, a3);
  not not_23 (not_23_out, a5);
  not not_24 (not_24_out, a0);
  not not_25 (not_25_out, a2);
  not not_26 (not_26_out, a5);
  not not_27 (not_27_out, a7);
  not not_28 (not_28_out, a0);
  not not_29 (not_29_out, a2);
  not not_30 (not_30_out, a4);
  not not_31 (not_31_out, a0);
  not not_32 (not_32_out, a1);
  not not_33 (not_33_out, a4);
  not not_34 (not_34_out, a5);
  not not_35 (not_35_out, a7);
  not not_36 (not_36_out, a0);
  not not_37 (not_37_out, a1);
  not not_38 (not_38_out, a4);
  not not_39 (not_39_out, a5);
  not not_40 (not_40_out, a0);
  not not_41 (not_41_out, a1);
  not not_42 (not_42_out, a4);
  not not_43 (not_43_out, a7);
  not not_44 (not_44_out, a0);
  not not_45 (not_45_out, a1);
  not not_46 (not_46_out, a4);
  not not_47 (not_47_out, a6);
  not not_48 (not_48_out, a0);
  not not_49 (not_49_out, a1);
  not not_50 (not_50_out, a5);
  not not_51 (not_51_out, a6);
  not not_52 (not_52_out, a0);
  not not_53 (not_53_out, a2);
  not not_54 (not_54_out, a4);
  not not_55 (not_55_out, a0);
  not not_56 (not_56_out, a2);
  not not_57 (not_57_out, a4);
  not not_58 (not_58_out, a0);
  not not_59 (not_59_out, a2);
  not not_60 (not_60_out, a3);
  not not_61 (not_61_out, a0);
  not not_62 (not_62_out, a2);
  not not_63 (not_63_out, a3);
  not not_64 (not_64_out, a0);
  not not_65 (not_65_out, a2);
  not not_66 (not_66_out, a3);
  not not_67 (not_67_out, a6);
  not not_68 (not_68_out, a7);
  not not_69 (not_69_out, a0);
  not not_70 (not_70_out, a2);
  not not_71 (not_71_out, a5);
  not not_72 (not_72_out, a6);
  not not_73 (not_73_out, a0);
  not not_74 (not_74_out, a1);
  not not_75 (not_75_out, a5);
  not not_76 (not_76_out, a6);
  not not_77 (not_77_out, a7);
  not not_78 (not_78_out, a0);
  not not_79 (not_79_out, a1);
  not not_80 (not_80_out, a4);
  not not_81 (not_81_out, a6);
  not not_82 (not_82_out, a0);
  not not_83 (not_83_out, a1);
  not not_84 (not_84_out, a4);
  not not_85 (not_85_out, a7);
  not not_86 (not_86_out, a0);
  not not_87 (not_87_out, a1);
  not not_88 (not_88_out, a5);
  not not_89 (not_89_out, a6);
  not not_90 (not_90_out, a0);
  not not_91 (not_91_out, a2);
  not not_92 (not_92_out, a4);
  not not_93 (not_93_out, a0);
  not not_94 (not_94_out, a2);
  not not_95 (not_95_out, a4);
  not not_96 (not_96_out, a0);
  not not_97 (not_97_out, a2);
  not not_98 (not_98_out, a3);
  not not_99 (not_99_out, a0);
  not not_100 (not_100_out, a2);
  not not_101 (not_101_out, a3);
  not not_102 (not_102_out, a0);
  not not_103 (not_103_out, a2);
  not not_104 (not_104_out, a3);
  not not_105 (not_105_out, a6);
  not not_106 (not_106_out, a7);
  not not_107 (not_107_out, a0);
  not not_108 (not_108_out, a2);
  not not_109 (not_109_out, a4);
  not not_110 (not_110_out, a5);
  not not_111 (not_111_out, a0);
  not not_112 (not_112_out, a1);
  not not_113 (not_113_out, a4);
  not not_114 (not_114_out, a6);
  not not_115 (not_115_out, a7);
  not not_116 (not_116_out, a0);
  not not_117 (not_117_out, a1);
  not not_118 (not_118_out, a4);
  not not_119 (not_119_out, a7);
  not not_120 (not_120_out, a0);
  not not_121 (not_121_out, a2);
  not not_122 (not_122_out, a4);
  not not_123 (not_123_out, a0);
  not not_124 (not_124_out, a2);
  not not_125 (not_125_out, a4);
  not not_126 (not_126_out, a0);
  not not_127 (not_127_out, a2);
  not not_128 (not_128_out, a3);
  not not_129 (not_129_out, a0);
  not not_130 (not_130_out, a2);
  not not_131 (not_131_out, a3);
  not not_132 (not_132_out, a0);
  not not_133 (not_133_out, a2);
  not not_134 (not_134_out, a3);
  not not_135 (not_135_out, a6);
  not not_136 (not_136_out, a7);
  not not_137 (not_137_out, a0);
  not not_138 (not_138_out, a2);
  not not_139 (not_139_out, a4);
  not not_140 (not_140_out, a5);
  not not_141 (not_141_out, a0);
  not not_142 (not_142_out, a1);
  not not_143 (not_143_out, a5);
  not not_144 (not_144_out, a6);
  not not_145 (not_145_out, a7);
  not not_146 (not_146_out, a0);
  not not_147 (not_147_out, a1);
  not not_148 (not_148_out, a4);
  not not_149 (not_149_out, a7);
  not not_150 (not_150_out, a0);
  not not_151 (not_151_out, a2);
  not not_152 (not_152_out, a4);
  not not_153 (not_153_out, a6);
  not not_154 (not_154_out, a0);
  not not_155 (not_155_out, a2);
  not not_156 (not_156_out, a3);
  not not_157 (not_157_out, a0);
  not not_158 (not_158_out, a2);
  not not_159 (not_159_out, a3);
  not not_160 (not_160_out, a0);
  not not_161 (not_161_out, a2);
  not not_162 (not_162_out, a4);
  not not_163 (not_163_out, a0);
  not not_164 (not_164_out, a2);
  not not_165 (not_165_out, a3);
  not not_166 (not_166_out, a7);
  not not_167 (not_167_out, a0);
  not not_168 (not_168_out, a2);
  not not_169 (not_169_out, a4);
  not not_170 (not_170_out, a5);
  not not_171 (not_171_out, a7);
  not not_172 (not_172_out, a0);
  not not_173 (not_173_out, a1);
  not not_174 (not_174_out, a5);
  not not_175 (not_175_out, a6);
  not not_176 (not_176_out, a7);
  not not_177 (not_177_out, a0);
  not not_178 (not_178_out, a1);
  not not_179 (not_179_out, a4);
  not not_180 (not_180_out, a5);
  not not_181 (not_181_out, a0);
  not not_182 (not_182_out, a1);
  not not_183 (not_183_out, a4);
  not not_184 (not_184_out, a6);
  not not_185 (not_185_out, a0);
  not not_186 (not_186_out, a1);
  not not_187 (not_187_out, a4);
  not not_188 (not_188_out, a7);
  not not_189 (not_189_out, a0);
  not not_190 (not_190_out, a1);
  not not_191 (not_191_out, a5);
  not not_192 (not_192_out, a6);
  not not_193 (not_193_out, a0);
  not not_194 (not_194_out, a2);
  not not_195 (not_195_out, a4);
  not not_196 (not_196_out, a6);
  not not_197 (not_197_out, a0);
  not not_198 (not_198_out, a2);
  not not_199 (not_199_out, a3);
  not not_200 (not_200_out, a0);
  not not_201 (not_201_out, a2);
  not not_202 (not_202_out, a3);
  not not_203 (not_203_out, a0);
  not not_204 (not_204_out, a2);
  not not_205 (not_205_out, a4);
  not not_206 (not_206_out, a0);
  not not_207 (not_207_out, a2);
  not not_208 (not_208_out, a3);
  not not_209 (not_209_out, a7);
  not not_210 (not_210_out, a0);
  not not_211 (not_211_out, a2);
  not not_212 (not_212_out, a5);
  not not_213 (not_213_out, a7);
  not not_214 (not_214_out, a0);
  not not_215 (not_215_out, a1);
  not not_216 (not_216_out, a4);
  not not_217 (not_217_out, a5);
  not not_218 (not_218_out, a7);
  not not_219 (not_219_out, a0);
  not not_220 (not_220_out, a2);
  not not_221 (not_221_out, a3);
  not not_222 (not_222_out, a6);
  not not_223 (not_223_out, a0);
  not not_224 (not_224_out, a2);
  not not_225 (not_225_out, a3);
  not not_226 (not_226_out, a4);
  not not_227 (not_227_out, a7);
  not not_228 (not_228_out, a0);
  not not_229 (not_229_out, a2);
  not not_230 (not_230_out, a3);
  not not_231 (not_231_out, a7);
  not not_232 (not_232_out, a0);
  not not_233 (not_233_out, a2);
  not not_234 (not_234_out, a3);
  not not_235 (not_235_out, a6);
  not not_236 (not_236_out, a0);
  not not_237 (not_237_out, a2);
  not not_238 (not_238_out, a3);
  not not_239 (not_239_out, a5);
  not not_240 (not_240_out, a0);
  not not_241 (not_241_out, a2);
  not not_242 (not_242_out, a5);
  not not_243 (not_243_out, a7);
  not not_244 (not_244_out, a0);
  not not_245 (not_245_out, a2);
  not not_246 (not_246_out, a4);
  and and_1 (and_1_out, not_1_out, not_2_out, a2, a3, not_3_out, a5, a7);
  and and_2 (and_2_out, not_4_out, a1, not_5_out, not_6_out, a6, not_7_out);
  and and_3 (and_3_out, not_8_out, a1, not_9_out, not_10_out, a5, not_11_out);
  and and_4 (and_4_out, not_12_out, a1, not_13_out, not_14_out, a5, not_15_out);
  and and_5 (and_5_out, not_16_out, a1, not_17_out, a4, not_18_out, not_19_out);
  and and_6 (and_6_out, not_20_out, a1, not_21_out, not_22_out, a4, not_23_out, a7);
  and and_7 (and_7_out, not_24_out, a1, not_25_out, a3, not_26_out, not_27_out);
  and and_8 (and_8_out, not_28_out, a1, not_29_out, a3, not_30_out, a5);
  and and_9 (and_9_out, not_31_out, not_32_out, a2, a3, not_33_out, not_34_out, not_35_out);
  and and_10 (and_10_out, not_36_out, not_37_out, a2, a3, not_38_out, not_39_out, a6);
  and and_11 (and_11_out, not_40_out, not_41_out, a2, a3, not_42_out, a6, not_43_out);
  and and_12 (and_12_out, not_44_out, not_45_out, a2, a3, not_46_out, a5, not_47_out, a7);
  and and_13 (and_13_out, not_48_out, not_49_out, a2, a3, a4, not_50_out, not_51_out);
  and and_14 (and_14_out, not_52_out, a1, not_53_out, not_54_out, a7);
  and and_15 (and_15_out, not_55_out, a1, not_56_out, not_57_out, a6);
  and and_16 (and_16_out, not_58_out, a1, not_59_out, not_60_out, a6, a7);
  and and_17 (and_17_out, not_61_out, a1, not_62_out, not_63_out, a5);
  and and_18 (and_18_out, not_64_out, a1, not_65_out, not_66_out, a4, not_67_out, not_68_out);
  and and_19 (and_19_out, not_69_out, a1, not_70_out, a3, not_71_out, not_72_out);
  and and_20 (and_20_out, not_73_out, not_74_out, a2, a3, not_75_out, not_76_out, not_77_out);
  and and_21 (and_21_out, not_78_out, not_79_out, a2, a3, not_80_out, a5, not_81_out, a7);
  and and_22 (and_22_out, not_82_out, not_83_out, a2, a3, not_84_out, a5, a6, not_85_out);
  and and_23 (and_23_out, not_86_out, not_87_out, a2, a3, a4, not_88_out, not_89_out);
  and and_24 (and_24_out, not_90_out, a1, not_91_out, not_92_out, a7);
  and and_25 (and_25_out, not_93_out, a1, not_94_out, not_95_out, a6);
  and and_26 (and_26_out, not_96_out, a1, not_97_out, not_98_out, a6, a7);
  and and_27 (and_27_out, not_99_out, a1, not_100_out, not_101_out, a5);
  and and_28 (and_28_out, not_102_out, a1, not_103_out, not_104_out, a4, not_105_out, not_106_out);
  and and_29 (and_29_out, not_107_out, a1, not_108_out, a3, not_109_out, not_110_out);
  and and_30 (and_30_out, not_111_out, not_112_out, a2, a3, not_113_out, not_114_out, not_115_out);
  and and_31 (and_31_out, not_116_out, not_117_out, a2, a3, not_118_out, a5, not_119_out);
  and and_32 (and_32_out, not_120_out, a1, not_121_out, not_122_out, a7);
  and and_33 (and_33_out, not_123_out, a1, not_124_out, not_125_out, a6);
  and and_34 (and_34_out, not_126_out, a1, not_127_out, not_128_out, a6, a7);
  and and_35 (and_35_out, not_129_out, a1, not_130_out, not_131_out, a5);
  and and_36 (and_36_out, not_132_out, a1, not_133_out, not_134_out, a4, not_135_out, not_136_out);
  and and_37 (and_37_out, not_137_out, a1, not_138_out, a3, not_139_out, not_140_out);
  and and_38 (and_38_out, not_141_out, not_142_out, a2, a3, not_143_out, not_144_out, not_145_out);
  and and_39 (and_39_out, not_146_out, not_147_out, a2, a3, not_148_out, a5, not_149_out);
  and and_40 (and_40_out, not_150_out, a1, not_151_out, not_152_out, not_153_out, a7);
  and and_41 (and_41_out, not_154_out, a1, not_155_out, not_156_out, a6);
  and and_42 (and_42_out, not_157_out, a1, not_158_out, not_159_out, a5);
  and and_43 (and_43_out, not_160_out, a1, not_161_out, not_162_out, a5, a6);
  and and_44 (and_44_out, not_163_out, a1, not_164_out, not_165_out, a4, not_166_out);
  and and_45 (and_45_out, not_167_out, a1, not_168_out, a3, not_169_out, not_170_out, not_171_out);
  and and_46 (and_46_out, not_172_out, not_173_out, a2, a3, not_174_out, not_175_out, not_176_out);
  and and_47 (and_47_out, not_177_out, not_178_out, a2, a3, not_179_out, not_180_out, a6, a7);
  and and_48 (and_48_out, not_181_out, not_182_out, a2, a3, not_183_out, a5, not_184_out, a7);
  and and_49 (and_49_out, not_185_out, not_186_out, a2, a3, not_187_out, a5, a6, not_188_out);
  and and_50 (and_50_out, not_189_out, not_190_out, a2, a3, a4, not_191_out, not_192_out);
  and and_51 (and_51_out, not_193_out, a1, not_194_out, not_195_out, not_196_out, a7);
  and and_52 (and_52_out, not_197_out, a1, not_198_out, not_199_out, a6);
  and and_53 (and_53_out, not_200_out, a1, not_201_out, not_202_out, a5);
  and and_54 (and_54_out, not_203_out, a1, not_204_out, not_205_out, a5, a7);
  and and_55 (and_55_out, not_206_out, a1, not_207_out, not_208_out, a4, not_209_out);
  and and_56 (and_56_out, not_210_out, a1, not_211_out, a3, not_212_out, not_213_out);
  and and_57 (and_57_out, not_214_out, not_215_out, a2, a3, not_216_out, not_217_out, a6, not_218_out);
  and and_58 (and_58_out, not_219_out, a1, not_220_out, not_221_out, not_222_out, a7);
  and and_59 (and_59_out, not_223_out, a1, not_224_out, not_225_out, not_226_out, a6, not_227_out);
  and and_60 (and_60_out, not_228_out, a1, not_229_out, not_230_out, a5, not_231_out);
  and and_61 (and_61_out, not_232_out, a1, not_233_out, not_234_out, a4, not_235_out);
  and and_62 (and_62_out, not_236_out, a1, not_237_out, not_238_out, a4, not_239_out, a7);
  and and_63 (and_63_out, not_240_out, a1, not_241_out, a3, not_242_out, not_243_out);
  and and_64 (and_64_out, not_244_out, a1, not_245_out, a3, not_246_out, a6, a7);
  or or_1 (x00, and_1_out, and_2_out, and_3_out, and_4_out, and_5_out, and_6_out, and_7_out, and_8_out);
  or or_2 (x10, and_9_out, and_10_out, and_11_out, and_12_out, and_13_out, and_14_out, and_15_out, and_16_out, and_17_out, and_18_out, and_19_out);
  or or_3 (x20, and_20_out, and_21_out, and_22_out, and_23_out, and_24_out, and_25_out, and_26_out, and_27_out, and_28_out, and_29_out);
  or or_4 (x30, and_30_out, and_31_out, and_32_out, and_33_out, and_34_out, and_35_out, and_36_out, and_37_out);
  or or_5 (x40, and_38_out, and_39_out, and_40_out, and_41_out, and_42_out, and_43_out, and_44_out, and_45_out);
  or or_6 (x50, and_46_out, and_47_out, and_48_out, and_49_out, and_50_out, and_51_out, and_52_out, and_53_out, and_54_out, and_55_out, and_56_out);
  or or_7 (x60, and_57_out, and_58_out, and_59_out, and_60_out, and_61_out, and_62_out, and_63_out, and_64_out);
endmodule

module COLUNA_1 (
  input  a0,
  input  a1,
  input  a2,
  input  a3,
  input  a4,
  input  a5,
  input  a6,
  input  a7,
  output x00,
  output x10,
  output x20,
  output x30,
  output x40,
  output x50,
  output x60
);

  wire and_1_out, and_2_out, and_3_out, and_4_out, and_5_out, and_6_out, and_7_out, and_8_out, and_9_out,
       and_10_out, and_11_out, and_12_out, and_13_out, and_14_out, and_15_out, and_16_out, and_17_out,
       and_18_out, and_19_out, and_20_out, and_21_out, and_22_out, and_23_out, and_24_out, and_25_out,
       and_26_out, and_27_out, and_28_out, and_29_out, and_30_out, and_31_out, and_32_out, and_33_out,
       and_34_out, and_35_out, and_36_out, and_37_out, and_38_out, and_39_out, and_40_out, and_41_out,
       not_1_out, not_2_out, not_3_out, not_4_out, not_5_out, not_6_out, not_7_out, not_8_out, not_9_out,
       not_10_out, not_11_out, not_12_out, not_13_out, not_14_out, not_15_out, not_16_out, not_17_out,
       not_18_out, not_19_out, not_20_out, not_21_out, not_22_out, not_23_out, not_24_out, not_25_out,
       not_26_out, not_27_out, not_28_out, not_29_out, not_30_out, not_31_out, not_32_out, not_33_out,
       not_34_out, not_35_out, not_36_out, not_37_out, not_38_out, not_39_out, not_40_out, not_41_out,
       not_42_out, not_43_out, not_44_out, not_45_out, not_46_out, not_47_out, not_48_out, not_49_out,
       not_50_out, not_51_out, not_52_out, not_53_out, not_54_out, not_55_out, not_56_out, not_57_out,
       not_58_out, not_59_out, not_60_out, not_61_out, not_62_out, not_63_out, not_64_out, not_65_out,
       not_66_out, not_67_out, not_68_out, not_69_out, not_70_out, not_71_out, not_72_out, not_73_out,
       not_74_out, not_75_out, not_76_out, not_77_out, not_78_out, not_79_out, not_80_out, not_81_out,
       not_82_out, not_83_out, not_84_out, not_85_out, not_86_out, not_87_out, not_88_out, not_89_out,
       not_90_out, not_91_out, not_92_out, not_93_out, not_94_out, not_95_out, not_96_out, not_97_out,
       not_98_out, not_99_out, not_100_out, not_101_out, not_102_out, not_103_out, not_104_out, not_105_out,
       not_106_out, not_107_out, not_108_out, not_109_out, not_110_out, not_111_out, not_112_out,
       not_113_out, not_114_out, not_115_out, not_116_out, not_117_out, not_118_out, not_119_out,
       not_120_out, not_121_out, not_122_out, not_123_out, not_124_out, not_125_out, not_126_out,
       not_127_out, not_128_out, not_129_out, not_130_out, not_131_out, not_132_out, not_133_out,
       not_134_out, not_135_out, not_136_out, not_137_out, not_138_out, not_139_out, not_140_out,
       not_141_out, not_142_out, not_143_out, not_144_out, not_145_out, not_146_out, not_147_out,
       not_148_out, not_149_out, not_150_out, not_151_out, not_152_out, not_153_out, not_154_out,
       not_155_out, not_156_out, not_157_out, not_158_out, not_159_out, not_160_out, not_161_out,
       not_162_out, not_163_out, not_164_out, not_165_out, not_166_out, not_167_out, not_168_out,
       not_169_out, not_170_out, not_171_out, not_172_out, not_173_out, not_174_out;

  not not_1 (not_1_out, a0);
  not not_2 (not_2_out, a1);
  not not_3 (not_3_out, a4);
  not not_4 (not_4_out, a5);
  not not_5 (not_5_out, a7);
  not not_6 (not_6_out, a0);
  not not_7 (not_7_out, a1);
  not not_8 (not_8_out, a4);
  not not_9 (not_9_out, a0);
  not not_10 (not_10_out, a1);
  not not_11 (not_11_out, a4);
  not not_12 (not_12_out, a0);
  not not_13 (not_13_out, a1);
  not not_14 (not_14_out, a5);
  not not_15 (not_15_out, a6);
  not not_16 (not_16_out, a0);
  not not_17 (not_17_out, a2);
  not not_18 (not_18_out, a3);
  not not_19 (not_19_out, a5);
  not not_20 (not_20_out, a6);
  not not_21 (not_21_out, a0);
  not not_22 (not_22_out, a2);
  not not_23 (not_23_out, a4);
  not not_24 (not_24_out, a5);
  not not_25 (not_25_out, a0);
  not not_26 (not_26_out, a2);
  not not_27 (not_27_out, a3);
  not not_28 (not_28_out, a4);
  not not_29 (not_29_out, a0);
  not not_30 (not_30_out, a2);
  not not_31 (not_31_out, a3);
  not not_32 (not_32_out, a0);
  not not_33 (not_33_out, a2);
  not not_34 (not_34_out, a4);
  not not_35 (not_35_out, a5);
  not not_36 (not_36_out, a0);
  not not_37 (not_37_out, a2);
  not not_38 (not_38_out, a4);
  not not_39 (not_39_out, a6);
  not not_40 (not_40_out, a7);
  not not_41 (not_41_out, a0);
  not not_42 (not_42_out, a2);
  not not_43 (not_43_out, a5);
  not not_44 (not_44_out, a7);
  not not_45 (not_45_out, a0);
  not not_46 (not_46_out, a1);
  not not_47 (not_47_out, a4);
  not not_48 (not_48_out, a5);
  not not_49 (not_49_out, a6);
  not not_50 (not_50_out, a0);
  not not_51 (not_51_out, a2);
  not not_52 (not_52_out, a3);
  not not_53 (not_53_out, a6);
  not not_54 (not_54_out, a0);
  not not_55 (not_55_out, a1);
  not not_56 (not_56_out, a4);
  not not_57 (not_57_out, a6);
  not not_58 (not_58_out, a0);
  not not_59 (not_59_out, a2);
  not not_60 (not_60_out, a3);
  not not_61 (not_61_out, a7);
  not not_62 (not_62_out, a0);
  not not_63 (not_63_out, a2);
  not not_64 (not_64_out, a5);
  not not_65 (not_65_out, a6);
  not not_66 (not_66_out, a0);
  not not_67 (not_67_out, a1);
  not not_68 (not_68_out, a4);
  not not_69 (not_69_out, a7);
  not not_70 (not_70_out, a0);
  not not_71 (not_71_out, a1);
  not not_72 (not_72_out, a5);
  not not_73 (not_73_out, a6);
  not not_74 (not_74_out, a0);
  not not_75 (not_75_out, a2);
  not not_76 (not_76_out, a3);
  not not_77 (not_77_out, a4);
  not not_78 (not_78_out, a6);
  not not_79 (not_79_out, a0);
  not not_80 (not_80_out, a2);
  not not_81 (not_81_out, a3);
  not not_82 (not_82_out, a4);
  not not_83 (not_83_out, a7);
  not not_84 (not_84_out, a0);
  not not_85 (not_85_out, a2);
  not not_86 (not_86_out, a3);
  not not_87 (not_87_out, a5);
  not not_88 (not_88_out, a6);
  not not_89 (not_89_out, a7);
  not not_90 (not_90_out, a0);
  not not_91 (not_91_out, a2);
  not not_92 (not_92_out, a3);
  not not_93 (not_93_out, a5);
  not not_94 (not_94_out, a0);
  not not_95 (not_95_out, a2);
  not not_96 (not_96_out, a4);
  not not_97 (not_97_out, a5);
  not not_98 (not_98_out, a7);
  not not_99 (not_99_out, a0);
  not not_100 (not_100_out, a2);
  not not_101 (not_101_out, a4);
  not not_102 (not_102_out, a5);
  not not_103 (not_103_out, a0);
  not not_104 (not_104_out, a1);
  not not_105 (not_105_out, a4);
  not not_106 (not_106_out, a6);
  not not_107 (not_107_out, a7);
  not not_108 (not_108_out, a0);
  not not_109 (not_109_out, a2);
  not not_110 (not_110_out, a5);
  not not_111 (not_111_out, a7);
  not not_112 (not_112_out, a0);
  not not_113 (not_113_out, a1);
  not not_114 (not_114_out, a4);
  not not_115 (not_115_out, a5);
  not not_116 (not_116_out, a7);
  not not_117 (not_117_out, a0);
  not not_118 (not_118_out, a2);
  not not_119 (not_119_out, a4);
  not not_120 (not_120_out, a0);
  not not_121 (not_121_out, a1);
  not not_122 (not_122_out, a4);
  not not_123 (not_123_out, a5);
  not not_124 (not_124_out, a7);
  not not_125 (not_125_out, a0);
  not not_126 (not_126_out, a1);
  not not_127 (not_127_out, a4);
  not not_128 (not_128_out, a5);
  not not_129 (not_129_out, a0);
  not not_130 (not_130_out, a1);
  not not_131 (not_131_out, a4);
  not not_132 (not_132_out, a7);
  not not_133 (not_133_out, a0);
  not not_134 (not_134_out, a1);
  not not_135 (not_135_out, a4);
  not not_136 (not_136_out, a6);
  not not_137 (not_137_out, a0);
  not not_138 (not_138_out, a1);
  not not_139 (not_139_out, a5);
  not not_140 (not_140_out, a6);
  not not_141 (not_141_out, a0);
  not not_142 (not_142_out, a2);
  not not_143 (not_143_out, a3);
  not not_144 (not_144_out, a5);
  not not_145 (not_145_out, a7);
  not not_146 (not_146_out, a0);
  not not_147 (not_147_out, a2);
  not not_148 (not_148_out, a4);
  not not_149 (not_149_out, a5);
  not not_150 (not_150_out, a0);
  not not_151 (not_151_out, a2);
  not not_152 (not_152_out, a3);
  not not_153 (not_153_out, a6);
  not not_154 (not_154_out, a7);
  not not_155 (not_155_out, a0);
  not not_156 (not_156_out, a2);
  not not_157 (not_157_out, a3);
  not not_158 (not_158_out, a4);
  not not_159 (not_159_out, a0);
  not not_160 (not_160_out, a2);
  not not_161 (not_161_out, a3);
  not not_162 (not_162_out, a0);
  not not_163 (not_163_out, a2);
  not not_164 (not_164_out, a3);
  not not_165 (not_165_out, a5);
  not not_166 (not_166_out, a6);
  not not_167 (not_167_out, a0);
  not not_168 (not_168_out, a2);
  not not_169 (not_169_out, a5);
  not not_170 (not_170_out, a7);
  not not_171 (not_171_out, a0);
  not not_172 (not_172_out, a2);
  not not_173 (not_173_out, a4);
  not not_174 (not_174_out, a6);
  and and_1 (and_1_out, not_1_out, not_2_out, a2, a3, not_3_out, not_4_out, not_5_out);
  and and_2 (and_2_out, not_6_out, not_7_out, a2, a3, not_8_out, a6);
  and and_3 (and_3_out, not_9_out, not_10_out, a2, a3, not_11_out, a5, a7);
  and and_4 (and_4_out, not_12_out, not_13_out, a2, a3, a4, not_14_out, not_15_out);
  and and_5 (and_5_out, not_16_out, a1, not_17_out, not_18_out, not_19_out, not_20_out, a7);
  and and_6 (and_6_out, not_21_out, a1, not_22_out, not_23_out, not_24_out, a6);
  and and_7 (and_7_out, not_25_out, a1, not_26_out, not_27_out, not_28_out, a5);
  and and_8 (and_8_out, not_29_out, a1, not_30_out, not_31_out, a5, a6, a7);
  and and_9 (and_9_out, not_32_out, a1, not_33_out, a3, not_34_out, not_35_out);
  and and_10 (and_10_out, not_36_out, a1, not_37_out, a3, not_38_out, not_39_out, not_40_out);
  and and_11 (and_11_out, not_41_out, a1, not_42_out, a3, not_43_out, a6, not_44_out);
  and and_12 (and_12_out, not_45_out, not_46_out, a2, a3, not_47_out, not_48_out, not_49_out, a7);
  and and_13 (and_13_out, not_50_out, a1, not_51_out, not_52_out, a4, a5, not_53_out, a7);
  and and_14 (and_14_out, not_54_out, not_55_out, a2, a3, not_56_out, a5, not_57_out);
  and and_15 (and_15_out, not_58_out, a1, not_59_out, not_60_out, a4, a5, a6, not_61_out);
  and and_16 (and_16_out, not_62_out, a1, not_63_out, a3, a4, not_64_out, not_65_out);
  and and_17 (and_17_out, not_66_out, not_67_out, a2, a3, not_68_out, a5, a6, not_69_out);
  and and_18 (and_18_out, not_70_out, not_71_out, a2, a3, a4, not_72_out, not_73_out);
  and and_19 (and_19_out, not_74_out, a1, not_75_out, not_76_out, not_77_out, not_78_out, a7);
  and and_20 (and_20_out, not_79_out, a1, not_80_out, not_81_out, not_82_out, a6, not_83_out);
  and and_21 (and_21_out, not_84_out, a1, not_85_out, not_86_out, a4, not_87_out, not_88_out, not_89_out);
  and and_22 (and_22_out, not_90_out, a1, not_91_out, not_92_out, a4, not_93_out, a6, a7);
  and and_23 (and_23_out, not_94_out, a1, not_95_out, a3, not_96_out, not_97_out, not_98_out);
  and and_24 (and_24_out, not_99_out, a1, not_100_out, a3, not_101_out, not_102_out, a6);
  and and_25 (and_25_out, not_103_out, not_104_out, a2, a3, not_105_out, a5, not_106_out, not_107_out);
  and and_26 (and_26_out, not_108_out, a1, not_109_out, a3, a4, not_110_out, not_111_out);
  and and_27 (and_27_out, not_112_out, not_113_out, a2, a3, not_114_out, not_115_out, a6, not_116_out);
  and and_28 (and_28_out, not_117_out, a1, not_118_out, a3, not_119_out, a5, a6);
  and and_29 (and_29_out, not_120_out, not_121_out, a2, a3, not_122_out, not_123_out, not_124_out);
  and and_30 (and_30_out, not_125_out, not_126_out, a2, a3, not_127_out, not_128_out, a6);
  and and_31 (and_31_out, not_129_out, not_130_out, a2, a3, not_131_out, a6, not_132_out);
  and and_32 (and_32_out, not_133_out, not_134_out, a2, a3, not_135_out, a5, not_136_out, a7);
  and and_33 (and_33_out, not_137_out, not_138_out, a2, a3, a4, not_139_out, not_140_out);
  and and_34 (and_34_out, not_141_out, a1, not_142_out, not_143_out, not_144_out, a6, not_145_out);
  and and_35 (and_35_out, not_146_out, a1, not_147_out, not_148_out, not_149_out, a6, a7);
  and and_36 (and_36_out, not_150_out, a1, not_151_out, not_152_out, a5, not_153_out, not_154_out);
  and and_37 (and_37_out, not_155_out, a1, not_156_out, not_157_out, not_158_out, a5, a7);
  and and_38 (and_38_out, not_159_out, a1, not_160_out, not_161_out, a5, a6, a7);
  and and_39 (and_39_out, not_162_out, a1, not_163_out, not_164_out, a4, not_165_out, not_166_out, a7);
  and and_40 (and_40_out, not_167_out, a1, not_168_out, a4, not_169_out, a6, not_170_out);
  and and_41 (and_41_out, not_171_out, a1, not_172_out, a3, not_173_out, not_174_out, a7);
  or or_1 (x00, and_1_out, and_2_out, and_3_out, and_4_out, and_5_out, and_6_out, and_7_out, and_8_out, and_9_out, and_10_out, and_11_out);
  or or_2 (x10, and_12_out, and_13_out);
  or or_3 (x20, and_14_out, and_15_out, and_16_out);
  or or_4 (x30, and_17_out, and_18_out, and_19_out, and_20_out, and_21_out, and_22_out, and_23_out, and_24_out);
  or or_5 (x40, and_25_out, and_26_out);
  or or_6 (x50, and_27_out, and_28_out);
  or or_7 (x60, and_29_out, and_30_out, and_31_out, and_32_out, and_33_out, and_34_out, and_35_out, and_36_out, and_37_out, and_38_out, and_39_out, and_40_out, and_41_out);
endmodule

module COLUNA_2 (
  input  a0,
  input  a1,
  input  a2,
  input  a3,
  input  a4,
  input  a5,
  input  a6,
  input  a7,
  output x00,
  output x10,
  output x20,
  output x30,
  output x40,
  output x50,
  output x60
);

  wire and_1_out, and_2_out, and_3_out, and_4_out, and_5_out, and_6_out, and_7_out, and_8_out, and_9_out,
       and_10_out, and_11_out, and_12_out, and_13_out, and_14_out, and_15_out, and_16_out, and_17_out,
       and_18_out, and_19_out, and_20_out, and_21_out, and_22_out, and_23_out, and_24_out, and_25_out,
       and_26_out, and_27_out, and_28_out, and_29_out, and_30_out, and_31_out, and_32_out, and_33_out,
       and_34_out, and_35_out, and_36_out, and_37_out, and_38_out, and_39_out, and_40_out, and_41_out,
       and_42_out, and_43_out, and_44_out, and_45_out, and_46_out, and_47_out, and_48_out, and_49_out,
       and_50_out, and_51_out, and_52_out, and_53_out, and_54_out, not_1_out, not_2_out, not_3_out,
       not_4_out, not_5_out, not_6_out, not_7_out, not_8_out, not_9_out, not_10_out, not_11_out, not_12_out,
       not_13_out, not_14_out, not_15_out, not_16_out, not_17_out, not_18_out, not_19_out, not_20_out,
       not_21_out, not_22_out, not_23_out, not_24_out, not_25_out, not_26_out, not_27_out, not_28_out,
       not_29_out, not_30_out, not_31_out, not_32_out, not_33_out, not_34_out, not_35_out, not_36_out,
       not_37_out, not_38_out, not_39_out, not_40_out, not_41_out, not_42_out, not_43_out, not_44_out,
       not_45_out, not_46_out, not_47_out, not_48_out, not_49_out, not_50_out, not_51_out, not_52_out,
       not_53_out, not_54_out, not_55_out, not_56_out, not_57_out, not_58_out, not_59_out, not_60_out,
       not_61_out, not_62_out, not_63_out, not_64_out, not_65_out, not_66_out, not_67_out, not_68_out,
       not_69_out, not_70_out, not_71_out, not_72_out, not_73_out, not_74_out, not_75_out, not_76_out,
       not_77_out, not_78_out, not_79_out, not_80_out, not_81_out, not_82_out, not_83_out, not_84_out,
       not_85_out, not_86_out, not_87_out, not_88_out, not_89_out, not_90_out, not_91_out, not_92_out,
       not_93_out, not_94_out, not_95_out, not_96_out, not_97_out, not_98_out, not_99_out, not_100_out,
       not_101_out, not_102_out, not_103_out, not_104_out, not_105_out, not_106_out, not_107_out,
       not_108_out, not_109_out, not_110_out, not_111_out, not_112_out, not_113_out, not_114_out,
       not_115_out, not_116_out, not_117_out, not_118_out, not_119_out, not_120_out, not_121_out,
       not_122_out, not_123_out, not_124_out, not_125_out, not_126_out, not_127_out, not_128_out,
       not_129_out, not_130_out, not_131_out, not_132_out, not_133_out, not_134_out, not_135_out,
       not_136_out, not_137_out, not_138_out, not_139_out, not_140_out, not_141_out, not_142_out,
       not_143_out, not_144_out, not_145_out, not_146_out, not_147_out, not_148_out, not_149_out,
       not_150_out, not_151_out, not_152_out, not_153_out, not_154_out, not_155_out, not_156_out,
       not_157_out, not_158_out, not_159_out, not_160_out, not_161_out, not_162_out, not_163_out,
       not_164_out, not_165_out, not_166_out, not_167_out, not_168_out, not_169_out, not_170_out,
       not_171_out, not_172_out, not_173_out, not_174_out, not_175_out, not_176_out, not_177_out,
       not_178_out, not_179_out, not_180_out, not_181_out, not_182_out, not_183_out, not_184_out,
       not_185_out, not_186_out, not_187_out, not_188_out, not_189_out, not_190_out, not_191_out,
       not_192_out, not_193_out, not_194_out, not_195_out, not_196_out, not_197_out, not_198_out,
       not_199_out, not_200_out, not_201_out, not_202_out, not_203_out, not_204_out, not_205_out,
       not_206_out, not_207_out, not_208_out, not_209_out, not_210_out, not_211_out, not_212_out,
       not_213_out, not_214_out, not_215_out, not_216_out, not_217_out, not_218_out, not_219_out,
       not_220_out, not_221_out, not_222_out, not_223_out;

  not not_1 (not_1_out, a0);
  not not_2 (not_2_out, a1);
  not not_3 (not_3_out, a5);
  not not_4 (not_4_out, a6);
  not not_5 (not_5_out, a0);
  not not_6 (not_6_out, a1);
  not not_7 (not_7_out, a4);
  not not_8 (not_8_out, a0);
  not not_9 (not_9_out, a1);
  not not_10 (not_10_out, a4);
  not not_11 (not_11_out, a0);
  not not_12 (not_12_out, a2);
  not not_13 (not_13_out, a3);
  not not_14 (not_14_out, a5);
  not not_15 (not_15_out, a6);
  not not_16 (not_16_out, a0);
  not not_17 (not_17_out, a2);
  not not_18 (not_18_out, a4);
  not not_19 (not_19_out, a5);
  not not_20 (not_20_out, a0);
  not not_21 (not_21_out, a2);
  not not_22 (not_22_out, a3);
  not not_23 (not_23_out, a4);
  not not_24 (not_24_out, a0);
  not not_25 (not_25_out, a2);
  not not_26 (not_26_out, a3);
  not not_27 (not_27_out, a0);
  not not_28 (not_28_out, a2);
  not not_29 (not_29_out, a4);
  not not_30 (not_30_out, a5);
  not not_31 (not_31_out, a0);
  not not_32 (not_32_out, a2);
  not not_33 (not_33_out, a4);
  not not_34 (not_34_out, a6);
  not not_35 (not_35_out, a7);
  not not_36 (not_36_out, a0);
  not not_37 (not_37_out, a2);
  not not_38 (not_38_out, a5);
  not not_39 (not_39_out, a7);
  not not_40 (not_40_out, a0);
  not not_41 (not_41_out, a1);
  not not_42 (not_42_out, a4);
  not not_43 (not_43_out, a5);
  not not_44 (not_44_out, a6);
  not not_45 (not_45_out, a0);
  not not_46 (not_46_out, a1);
  not not_47 (not_47_out, a4);
  not not_48 (not_48_out, a6);
  not not_49 (not_49_out, a7);
  not not_50 (not_50_out, a0);
  not not_51 (not_51_out, a2);
  not not_52 (not_52_out, a3);
  not not_53 (not_53_out, a5);
  not not_54 (not_54_out, a6);
  not not_55 (not_55_out, a0);
  not not_56 (not_56_out, a2);
  not not_57 (not_57_out, a4);
  not not_58 (not_58_out, a6);
  not not_59 (not_59_out, a7);
  not not_60 (not_60_out, a0);
  not not_61 (not_61_out, a1);
  not not_62 (not_62_out, a4);
  not not_63 (not_63_out, a6);
  not not_64 (not_64_out, a0);
  not not_65 (not_65_out, a2);
  not not_66 (not_66_out, a3);
  not not_67 (not_67_out, a5);
  not not_68 (not_68_out, a0);
  not not_69 (not_69_out, a2);
  not not_70 (not_70_out, a3);
  not not_71 (not_71_out, a6);
  not not_72 (not_72_out, a0);
  not not_73 (not_73_out, a2);
  not not_74 (not_74_out, a4);
  not not_75 (not_75_out, a6);
  not not_76 (not_76_out, a7);
  not not_77 (not_77_out, a0);
  not not_78 (not_78_out, a1);
  not not_79 (not_79_out, a4);
  not not_80 (not_80_out, a5);
  not not_81 (not_81_out, a0);
  not not_82 (not_82_out, a1);
  not not_83 (not_83_out, a4);
  not not_84 (not_84_out, a0);
  not not_85 (not_85_out, a1);
  not not_86 (not_86_out, a5);
  not not_87 (not_87_out, a6);
  not not_88 (not_88_out, a0);
  not not_89 (not_89_out, a2);
  not not_90 (not_90_out, a3);
  not not_91 (not_91_out, a6);
  not not_92 (not_92_out, a0);
  not not_93 (not_93_out, a2);
  not not_94 (not_94_out, a3);
  not not_95 (not_95_out, a4);
  not not_96 (not_96_out, a7);
  not not_97 (not_97_out, a0);
  not not_98 (not_98_out, a2);
  not not_99 (not_99_out, a3);
  not not_100 (not_100_out, a7);
  not not_101 (not_101_out, a0);
  not not_102 (not_102_out, a2);
  not not_103 (not_103_out, a4);
  not not_104 (not_104_out, a0);
  not not_105 (not_105_out, a2);
  not not_106 (not_106_out, a5);
  not not_107 (not_107_out, a6);
  not not_108 (not_108_out, a0);
  not not_109 (not_109_out, a2);
  not not_110 (not_110_out, a4);
  not not_111 (not_111_out, a6);
  not not_112 (not_112_out, a7);
  not not_113 (not_113_out, a0);
  not not_114 (not_114_out, a2);
  not not_115 (not_115_out, a5);
  not not_116 (not_116_out, a7);
  not not_117 (not_117_out, a0);
  not not_118 (not_118_out, a2);
  not not_119 (not_119_out, a4);
  not not_120 (not_120_out, a5);
  not not_121 (not_121_out, a0);
  not not_122 (not_122_out, a1);
  not not_123 (not_123_out, a4);
  not not_124 (not_124_out, a5);
  not not_125 (not_125_out, a6);
  not not_126 (not_126_out, a0);
  not not_127 (not_127_out, a1);
  not not_128 (not_128_out, a4);
  not not_129 (not_129_out, a5);
  not not_130 (not_130_out, a7);
  not not_131 (not_131_out, a0);
  not not_132 (not_132_out, a1);
  not not_133 (not_133_out, a4);
  not not_134 (not_134_out, a6);
  not not_135 (not_135_out, a7);
  not not_136 (not_136_out, a0);
  not not_137 (not_137_out, a1);
  not not_138 (not_138_out, a4);
  not not_139 (not_139_out, a0);
  not not_140 (not_140_out, a2);
  not not_141 (not_141_out, a3);
  not not_142 (not_142_out, a5);
  not not_143 (not_143_out, a0);
  not not_144 (not_144_out, a2);
  not not_145 (not_145_out, a5);
  not not_146 (not_146_out, a6);
  not not_147 (not_147_out, a0);
  not not_148 (not_148_out, a2);
  not not_149 (not_149_out, a4);
  not not_150 (not_150_out, a5);
  not not_151 (not_151_out, a7);
  not not_152 (not_152_out, a0);
  not not_153 (not_153_out, a2);
  not not_154 (not_154_out, a4);
  not not_155 (not_155_out, a6);
  not not_156 (not_156_out, a7);
  not not_157 (not_157_out, a0);
  not not_158 (not_158_out, a2);
  not not_159 (not_159_out, a4);
  not not_160 (not_160_out, a0);
  not not_161 (not_161_out, a1);
  not not_162 (not_162_out, a4);
  not not_163 (not_163_out, a5);
  not not_164 (not_164_out, a6);
  not not_165 (not_165_out, a0);
  not not_166 (not_166_out, a1);
  not not_167 (not_167_out, a4);
  not not_168 (not_168_out, a0);
  not not_169 (not_169_out, a2);
  not not_170 (not_170_out, a5);
  not not_171 (not_171_out, a6);
  not not_172 (not_172_out, a0);
  not not_173 (not_173_out, a2);
  not not_174 (not_174_out, a4);
  not not_175 (not_175_out, a6);
  not not_176 (not_176_out, a7);
  not not_177 (not_177_out, a0);
  not not_178 (not_178_out, a1);
  not not_179 (not_179_out, a5);
  not not_180 (not_180_out, a6);
  not not_181 (not_181_out, a0);
  not not_182 (not_182_out, a1);
  not not_183 (not_183_out, a4);
  not not_184 (not_184_out, a0);
  not not_185 (not_185_out, a1);
  not not_186 (not_186_out, a4);
  not not_187 (not_187_out, a0);
  not not_188 (not_188_out, a2);
  not not_189 (not_189_out, a3);
  not not_190 (not_190_out, a5);
  not not_191 (not_191_out, a7);
  not not_192 (not_192_out, a0);
  not not_193 (not_193_out, a2);
  not not_194 (not_194_out, a4);
  not not_195 (not_195_out, a5);
  not not_196 (not_196_out, a0);
  not not_197 (not_197_out, a2);
  not not_198 (not_198_out, a3);
  not not_199 (not_199_out, a6);
  not not_200 (not_200_out, a7);
  not not_201 (not_201_out, a0);
  not not_202 (not_202_out, a2);
  not not_203 (not_203_out, a4);
  not not_204 (not_204_out, a6);
  not not_205 (not_205_out, a0);
  not not_206 (not_206_out, a2);
  not not_207 (not_207_out, a3);
  not not_208 (not_208_out, a0);
  not not_209 (not_209_out, a2);
  not not_210 (not_210_out, a5);
  not not_211 (not_211_out, a6);
  not not_212 (not_212_out, a0);
  not not_213 (not_213_out, a2);
  not not_214 (not_214_out, a5);
  not not_215 (not_215_out, a7);
  not not_216 (not_216_out, a0);
  not not_217 (not_217_out, a2);
  not not_218 (not_218_out, a4);
  not not_219 (not_219_out, a6);
  not not_220 (not_220_out, a0);
  not not_221 (not_221_out, a2);
  not not_222 (not_222_out, a4);
  not not_223 (not_223_out, a7);
  and and_1 (and_1_out, not_1_out, not_2_out, a2, a3, not_3_out, not_4_out);
  and and_2 (and_2_out, not_5_out, not_6_out, a2, a3, not_7_out, a7);
  and and_3 (and_3_out, not_8_out, not_9_out, a2, a3, not_10_out, a6);
  and and_4 (and_4_out, not_11_out, a1, not_12_out, not_13_out, not_14_out, not_15_out, a7);
  and and_5 (and_5_out, not_16_out, a1, not_17_out, not_18_out, not_19_out, a6);
  and and_6 (and_6_out, not_20_out, a1, not_21_out, not_22_out, not_23_out, a5);
  and and_7 (and_7_out, not_24_out, a1, not_25_out, not_26_out, a5, a6, a7);
  and and_8 (and_8_out, not_27_out, a1, not_28_out, a3, not_29_out, not_30_out);
  and and_9 (and_9_out, not_31_out, a1, not_32_out, a3, not_33_out, not_34_out, not_35_out);
  and and_10 (and_10_out, not_36_out, a1, not_37_out, a3, not_38_out, a6, not_39_out);
  and and_11 (and_11_out, not_40_out, not_41_out, a2, a3, not_42_out, not_43_out, not_44_out, a7);
  and and_12 (and_12_out, not_45_out, not_46_out, a2, a3, not_47_out, a5, not_48_out, not_49_out);
  and and_13 (and_13_out, not_50_out, a1, not_51_out, not_52_out, a4, not_53_out, not_54_out, a7);
  and and_14 (and_14_out, not_55_out, a1, not_56_out, a3, not_57_out, a5, not_58_out, not_59_out);
  and and_15 (and_15_out, not_60_out, not_61_out, a2, a3, not_62_out, not_63_out, a7);
  and and_16 (and_16_out, not_64_out, a1, not_65_out, not_66_out, a4, not_67_out, a7);
  and and_17 (and_17_out, not_68_out, a1, not_69_out, not_70_out, a4, not_71_out, a7);
  and and_18 (and_18_out, not_72_out, a1, not_73_out, a3, not_74_out, a5, not_75_out, not_76_out);
  and and_19 (and_19_out, not_77_out, not_78_out, a2, a3, not_79_out, not_80_out, a7);
  and and_20 (and_20_out, not_81_out, not_82_out, a2, a3, not_83_out, a5, a6);
  and and_21 (and_21_out, not_84_out, not_85_out, a2, a3, a4, not_86_out, not_87_out);
  and and_22 (and_22_out, not_88_out, a1, not_89_out, not_90_out, not_91_out, a7);
  and and_23 (and_23_out, not_92_out, a1, not_93_out, not_94_out, not_95_out, a6, not_96_out);
  and and_24 (and_24_out, not_97_out, a1, not_98_out, not_99_out, a5, a6, not_100_out);
  and and_25 (and_25_out, not_101_out, a1, not_102_out, not_103_out, a5, a6, a7);
  and and_26 (and_26_out, not_104_out, a1, not_105_out, a4, not_106_out, not_107_out);
  and and_27 (and_27_out, not_108_out, a1, not_109_out, a3, not_110_out, not_111_out, not_112_out);
  and and_28 (and_28_out, not_113_out, a1, not_114_out, a3, not_115_out, not_116_out);
  and and_29 (and_29_out, not_117_out, a1, not_118_out, a3, not_119_out, not_120_out, a6);
  and and_30 (and_30_out, not_121_out, not_122_out, a2, a3, not_123_out, not_124_out, not_125_out, a7);
  and and_31 (and_31_out, not_126_out, not_127_out, a2, a3, not_128_out, not_129_out, a6, not_130_out);
  and and_32 (and_32_out, not_131_out, not_132_out, a2, a3, not_133_out, a5, not_134_out, not_135_out);
  and and_33 (and_33_out, not_136_out, not_137_out, a2, a3, not_138_out, a5, a6, a7);
  and and_34 (and_34_out, not_139_out, a1, not_140_out, not_141_out, a4, not_142_out, a7);
  and and_35 (and_35_out, not_143_out, a1, not_144_out, a3, not_145_out, not_146_out, a7);
  and and_36 (and_36_out, not_147_out, a1, not_148_out, a3, not_149_out, not_150_out, a6, not_151_out);
  and and_37 (and_37_out, not_152_out, a1, not_153_out, a3, not_154_out, a5, not_155_out, not_156_out);
  and and_38 (and_38_out, not_157_out, a1, not_158_out, a3, not_159_out, a5, a6, a7);
  and and_39 (and_39_out, not_160_out, not_161_out, a2, a3, not_162_out, not_163_out, not_164_out, a7);
  and and_40 (and_40_out, not_165_out, not_166_out, a2, a3, not_167_out, a5, a6, a7);
  and and_41 (and_41_out, not_168_out, a1, not_169_out, a4, not_170_out, not_171_out, a7);
  and and_42 (and_42_out, not_172_out, a1, not_173_out, a3, not_174_out, a5, not_175_out, not_176_out);
  and and_43 (and_43_out, not_177_out, not_178_out, a2, a3, not_179_out, not_180_out);
  and and_44 (and_44_out, not_181_out, not_182_out, a2, a3, not_183_out, a7);
  and and_45 (and_45_out, not_184_out, not_185_out, a2, a3, not_186_out, a6);
  and and_46 (and_46_out, not_187_out, a1, not_188_out, not_189_out, not_190_out, a6, not_191_out);
  and and_47 (and_47_out, not_192_out, a1, not_193_out, not_194_out, not_195_out, a6, a7);
  and and_48 (and_48_out, not_196_out, a1, not_197_out, not_198_out, a5, not_199_out, not_200_out);
  and and_49 (and_49_out, not_201_out, a1, not_202_out, not_203_out, a5, not_204_out);
  and and_50 (and_50_out, not_205_out, a1, not_206_out, not_207_out, a5, a6, a7);
  and and_51 (and_51_out, not_208_out, a1, not_209_out, a4, not_210_out, not_211_out, a7);
  and and_52 (and_52_out, not_212_out, a1, not_213_out, a4, not_214_out, a6, not_215_out);
  and and_53 (and_53_out, not_216_out, a1, not_217_out, a3, not_218_out, not_219_out, a7);
  and and_54 (and_54_out, not_220_out, a1, not_221_out, a3, not_222_out, a5, not_223_out);
  or or_1 (x00, and_1_out, and_2_out, and_3_out, and_4_out, and_5_out, and_6_out, and_7_out, and_8_out, and_9_out, and_10_out);
  or or_2 (x10, and_11_out, and_12_out, and_13_out, and_14_out);
  or or_3 (x20, and_15_out, and_16_out, and_17_out, and_18_out);
  or or_4 (x30, and_19_out, and_20_out, and_21_out, and_22_out, and_23_out, and_24_out, and_25_out, and_26_out, and_27_out, and_28_out, and_29_out);
  or or_5 (x40, and_30_out, and_31_out, and_32_out, and_33_out, and_34_out, and_35_out, and_36_out, and_37_out, and_38_out);
  or or_6 (x50, and_39_out, and_40_out, and_41_out, and_42_out);
  or or_7 (x60, and_43_out, and_44_out, and_45_out, and_46_out, and_47_out, and_48_out, and_49_out, and_50_out, and_51_out, and_52_out, and_53_out, and_54_out);
endmodule

module COLUNA_3 (
  input  a0,
  input  a1,
  input  a2,
  input  a3,
  input  a4,
  input  a5,
  input  a6,
  input  a7,
  output x00,
  output x10,
  output x20,
  output x30,
  output x40,
  output x50,
  output x60
);

  wire and_1_out, and_2_out, and_3_out, and_4_out, and_5_out, and_6_out, and_7_out, and_8_out, and_9_out,
       and_10_out, and_11_out, and_12_out, and_13_out, and_14_out, and_15_out, and_16_out, and_17_out,
       and_18_out, and_19_out, and_20_out, and_21_out, and_22_out, and_23_out, and_24_out, and_25_out,
       and_26_out, and_27_out, and_28_out, and_29_out, and_30_out, and_31_out, and_32_out, and_33_out,
       and_34_out, and_35_out, and_36_out, and_37_out, and_38_out, and_39_out, and_40_out, and_41_out,
       and_42_out, and_43_out, and_44_out, and_45_out, and_46_out, and_47_out, not_1_out, not_2_out,
       not_3_out, not_4_out, not_5_out, not_6_out, not_7_out, not_8_out, not_9_out, not_10_out, not_11_out,
       not_12_out, not_13_out, not_14_out, not_15_out, not_16_out, not_17_out, not_18_out, not_19_out,
       not_20_out, not_21_out, not_22_out, not_23_out, not_24_out, not_25_out, not_26_out, not_27_out,
       not_28_out, not_29_out, not_30_out, not_31_out, not_32_out, not_33_out, not_34_out, not_35_out,
       not_36_out, not_37_out, not_38_out, not_39_out, not_40_out, not_41_out, not_42_out, not_43_out,
       not_44_out, not_45_out, not_46_out, not_47_out, not_48_out, not_49_out, not_50_out, not_51_out,
       not_52_out, not_53_out, not_54_out, not_55_out, not_56_out, not_57_out, not_58_out, not_59_out,
       not_60_out, not_61_out, not_62_out, not_63_out, not_64_out, not_65_out, not_66_out, not_67_out,
       not_68_out, not_69_out, not_70_out, not_71_out, not_72_out, not_73_out, not_74_out, not_75_out,
       not_76_out, not_77_out, not_78_out, not_79_out, not_80_out, not_81_out, not_82_out, not_83_out,
       not_84_out, not_85_out, not_86_out, not_87_out, not_88_out, not_89_out, not_90_out, not_91_out,
       not_92_out, not_93_out, not_94_out, not_95_out, not_96_out, not_97_out, not_98_out, not_99_out,
       not_100_out, not_101_out, not_102_out, not_103_out, not_104_out, not_105_out, not_106_out,
       not_107_out, not_108_out, not_109_out, not_110_out, not_111_out, not_112_out, not_113_out,
       not_114_out, not_115_out, not_116_out, not_117_out, not_118_out, not_119_out, not_120_out,
       not_121_out, not_122_out, not_123_out, not_124_out, not_125_out, not_126_out, not_127_out,
       not_128_out, not_129_out, not_130_out, not_131_out, not_132_out, not_133_out, not_134_out,
       not_135_out, not_136_out, not_137_out, not_138_out, not_139_out, not_140_out, not_141_out,
       not_142_out, not_143_out, not_144_out, not_145_out, not_146_out, not_147_out, not_148_out,
       not_149_out, not_150_out, not_151_out, not_152_out, not_153_out, not_154_out, not_155_out,
       not_156_out, not_157_out, not_158_out, not_159_out, not_160_out, not_161_out, not_162_out,
       not_163_out, not_164_out, not_165_out, not_166_out, not_167_out, not_168_out, not_169_out,
       not_170_out, not_171_out, not_172_out, not_173_out, not_174_out, not_175_out, not_176_out,
       not_177_out, not_178_out, not_179_out, not_180_out, not_181_out, not_182_out, not_183_out,
       not_184_out, not_185_out, not_186_out, not_187_out, not_188_out, not_189_out, not_190_out,
       not_191_out, not_192_out, not_193_out, not_194_out, not_195_out, not_196_out;

  not not_1 (not_1_out, a0);
  not not_2 (not_2_out, a1);
  not not_3 (not_3_out, a4);
  not not_4 (not_4_out, a7);
  not not_5 (not_5_out, a0);
  not not_6 (not_6_out, a1);
  not not_7 (not_7_out, a4);
  not not_8 (not_8_out, a0);
  not not_9 (not_9_out, a1);
  not not_10 (not_10_out, a4);
  not not_11 (not_11_out, a0);
  not not_12 (not_12_out, a1);
  not not_13 (not_13_out, a5);
  not not_14 (not_14_out, a6);
  not not_15 (not_15_out, a0);
  not not_16 (not_16_out, a2);
  not not_17 (not_17_out, a3);
  not not_18 (not_18_out, a4);
  not not_19 (not_19_out, a0);
  not not_20 (not_20_out, a2);
  not not_21 (not_21_out, a3);
  not not_22 (not_22_out, a5);
  not not_23 (not_23_out, a6);
  not not_24 (not_24_out, a0);
  not not_25 (not_25_out, a2);
  not not_26 (not_26_out, a5);
  not not_27 (not_27_out, a7);
  not not_28 (not_28_out, a0);
  not not_29 (not_29_out, a2);
  not not_30 (not_30_out, a3);
  not not_31 (not_31_out, a4);
  not not_32 (not_32_out, a0);
  not not_33 (not_33_out, a2);
  not not_34 (not_34_out, a3);
  not not_35 (not_35_out, a0);
  not not_36 (not_36_out, a2);
  not not_37 (not_37_out, a4);
  not not_38 (not_38_out, a5);
  not not_39 (not_39_out, a0);
  not not_40 (not_40_out, a2);
  not not_41 (not_41_out, a4);
  not not_42 (not_42_out, a6);
  not not_43 (not_43_out, a7);
  not not_44 (not_44_out, a0);
  not not_45 (not_45_out, a1);
  not not_46 (not_46_out, a4);
  not not_47 (not_47_out, a6);
  not not_48 (not_48_out, a7);
  not not_49 (not_49_out, a0);
  not not_50 (not_50_out, a2);
  not not_51 (not_51_out, a3);
  not not_52 (not_52_out, a5);
  not not_53 (not_53_out, a0);
  not not_54 (not_54_out, a2);
  not not_55 (not_55_out, a3);
  not not_56 (not_56_out, a6);
  not not_57 (not_57_out, a0);
  not not_58 (not_58_out, a1);
  not not_59 (not_59_out, a4);
  not not_60 (not_60_out, a6);
  not not_61 (not_61_out, a0);
  not not_62 (not_62_out, a1);
  not not_63 (not_63_out, a4);
  not not_64 (not_64_out, a0);
  not not_65 (not_65_out, a2);
  not not_66 (not_66_out, a5);
  not not_67 (not_67_out, a7);
  not not_68 (not_68_out, a0);
  not not_69 (not_69_out, a2);
  not not_70 (not_70_out, a5);
  not not_71 (not_71_out, a6);
  not not_72 (not_72_out, a0);
  not not_73 (not_73_out, a1);
  not not_74 (not_74_out, a4);
  not not_75 (not_75_out, a5);
  not not_76 (not_76_out, a0);
  not not_77 (not_77_out, a1);
  not not_78 (not_78_out, a4);
  not not_79 (not_79_out, a7);
  not not_80 (not_80_out, a0);
  not not_81 (not_81_out, a1);
  not not_82 (not_82_out, a5);
  not not_83 (not_83_out, a6);
  not not_84 (not_84_out, a0);
  not not_85 (not_85_out, a2);
  not not_86 (not_86_out, a3);
  not not_87 (not_87_out, a4);
  not not_88 (not_88_out, a6);
  not not_89 (not_89_out, a0);
  not not_90 (not_90_out, a2);
  not not_91 (not_91_out, a3);
  not not_92 (not_92_out, a4);
  not not_93 (not_93_out, a7);
  not not_94 (not_94_out, a0);
  not not_95 (not_95_out, a2);
  not not_96 (not_96_out, a3);
  not not_97 (not_97_out, a4);
  not not_98 (not_98_out, a0);
  not not_99 (not_99_out, a2);
  not not_100 (not_100_out, a3);
  not not_101 (not_101_out, a5);
  not not_102 (not_102_out, a7);
  not not_103 (not_103_out, a0);
  not not_104 (not_104_out, a2);
  not not_105 (not_105_out, a4);
  not not_106 (not_106_out, a5);
  not not_107 (not_107_out, a7);
  not not_108 (not_108_out, a0);
  not not_109 (not_109_out, a2);
  not not_110 (not_110_out, a4);
  not not_111 (not_111_out, a5);
  not not_112 (not_112_out, a0);
  not not_113 (not_113_out, a1);
  not not_114 (not_114_out, a4);
  not not_115 (not_115_out, a6);
  not not_116 (not_116_out, a7);
  not not_117 (not_117_out, a0);
  not not_118 (not_118_out, a2);
  not not_119 (not_119_out, a3);
  not not_120 (not_120_out, a7);
  not not_121 (not_121_out, a0);
  not not_122 (not_122_out, a2);
  not not_123 (not_123_out, a5);
  not not_124 (not_124_out, a6);
  not not_125 (not_125_out, a7);
  not not_126 (not_126_out, a0);
  not not_127 (not_127_out, a1);
  not not_128 (not_128_out, a4);
  not not_129 (not_129_out, a6);
  not not_130 (not_130_out, a7);
  not not_131 (not_131_out, a0);
  not not_132 (not_132_out, a2);
  not not_133 (not_133_out, a3);
  not not_134 (not_134_out, a5);
  not not_135 (not_135_out, a0);
  not not_136 (not_136_out, a2);
  not not_137 (not_137_out, a4);
  not not_138 (not_138_out, a5);
  not not_139 (not_139_out, a6);
  not not_140 (not_140_out, a0);
  not not_141 (not_141_out, a2);
  not not_142 (not_142_out, a4);
  not not_143 (not_143_out, a7);
  not not_144 (not_144_out, a0);
  not not_145 (not_145_out, a2);
  not not_146 (not_146_out, a4);
  not not_147 (not_147_out, a0);
  not not_148 (not_148_out, a1);
  not not_149 (not_149_out, a4);
  not not_150 (not_150_out, a7);
  not not_151 (not_151_out, a0);
  not not_152 (not_152_out, a1);
  not not_153 (not_153_out, a4);
  not not_154 (not_154_out, a5);
  not not_155 (not_155_out, a0);
  not not_156 (not_156_out, a1);
  not not_157 (not_157_out, a4);
  not not_158 (not_158_out, a6);
  not not_159 (not_159_out, a0);
  not not_160 (not_160_out, a1);
  not not_161 (not_161_out, a5);
  not not_162 (not_162_out, a6);
  not not_163 (not_163_out, a0);
  not not_164 (not_164_out, a2);
  not not_165 (not_165_out, a3);
  not not_166 (not_166_out, a4);
  not not_167 (not_167_out, a5);
  not not_168 (not_168_out, a0);
  not not_169 (not_169_out, a2);
  not not_170 (not_170_out, a4);
  not not_171 (not_171_out, a5);
  not not_172 (not_172_out, a0);
  not not_173 (not_173_out, a2);
  not not_174 (not_174_out, a3);
  not not_175 (not_175_out, a6);
  not not_176 (not_176_out, a7);
  not not_177 (not_177_out, a0);
  not not_178 (not_178_out, a2);
  not not_179 (not_179_out, a3);
  not not_180 (not_180_out, a4);
  not not_181 (not_181_out, a0);
  not not_182 (not_182_out, a2);
  not not_183 (not_183_out, a3);
  not not_184 (not_184_out, a0);
  not not_185 (not_185_out, a2);
  not not_186 (not_186_out, a3);
  not not_187 (not_187_out, a5);
  not not_188 (not_188_out, a6);
  not not_189 (not_189_out, a0);
  not not_190 (not_190_out, a2);
  not not_191 (not_191_out, a4);
  not not_192 (not_192_out, a6);
  not not_193 (not_193_out, a0);
  not not_194 (not_194_out, a2);
  not not_195 (not_195_out, a5);
  not not_196 (not_196_out, a7);
  and and_1 (and_1_out, not_1_out, not_2_out, a2, a3, not_3_out, not_4_out);
  and and_2 (and_2_out, not_5_out, not_6_out, a2, a3, not_7_out, a6);
  and and_3 (and_3_out, not_8_out, not_9_out, a2, a3, not_10_out, a5);
  and and_4 (and_4_out, not_11_out, not_12_out, a2, a3, a4, not_13_out, not_14_out);
  and and_5 (and_5_out, not_15_out, a1, not_16_out, not_17_out, not_18_out, a7);
  and and_6 (and_6_out, not_19_out, a1, not_20_out, not_21_out, not_22_out, not_23_out, a7);
  and and_7 (and_7_out, not_24_out, a1, not_25_out, not_26_out, a6, not_27_out);
  and and_8 (and_8_out, not_28_out, a1, not_29_out, not_30_out, not_31_out, a5);
  and and_9 (and_9_out, not_32_out, a1, not_33_out, not_34_out, a5, a6, a7);
  and and_10 (and_10_out, not_35_out, a1, not_36_out, a3, not_37_out, not_38_out);
  and and_11 (and_11_out, not_39_out, a1, not_40_out, a3, not_41_out, not_42_out, not_43_out);
  and and_12 (and_12_out, not_44_out, not_45_out, a2, a3, not_46_out, a5, not_47_out, not_48_out);
  and and_13 (and_13_out, not_49_out, a1, not_50_out, not_51_out, a4, not_52_out, a6);
  and and_14 (and_14_out, not_53_out, a1, not_54_out, not_55_out, a4, a5, not_56_out, a7);
  and and_15 (and_15_out, not_57_out, not_58_out, a2, a3, not_59_out, a5, not_60_out);
  and and_16 (and_16_out, not_61_out, not_62_out, a2, a3, not_63_out, a5, a7);
  and and_17 (and_17_out, not_64_out, a1, not_65_out, a4, not_66_out, a6, not_67_out);
  and and_18 (and_18_out, not_68_out, a1, not_69_out, a3, a4, not_70_out, not_71_out);
  and and_19 (and_19_out, not_72_out, not_73_out, a2, a3, not_74_out, not_75_out, a6);
  and and_20 (and_20_out, not_76_out, not_77_out, a2, a3, not_78_out, a5, not_79_out);
  and and_21 (and_21_out, not_80_out, not_81_out, a2, a3, a4, not_82_out, not_83_out);
  and and_22 (and_22_out, not_84_out, a1, not_85_out, not_86_out, not_87_out, not_88_out, a7);
  and and_23 (and_23_out, not_89_out, a1, not_90_out, not_91_out, not_92_out, a6, not_93_out);
  and and_24 (and_24_out, not_94_out, a1, not_95_out, not_96_out, not_97_out, a5, a6);
  and and_25 (and_25_out, not_98_out, a1, not_99_out, not_100_out, a4, not_101_out, not_102_out);
  and and_26 (and_26_out, not_103_out, a1, not_104_out, a3, not_105_out, not_106_out, not_107_out);
  and and_27 (and_27_out, not_108_out, a1, not_109_out, a3, not_110_out, not_111_out, a6);
  and and_28 (and_28_out, not_112_out, not_113_out, a2, a3, not_114_out, a5, not_115_out, not_116_out);
  and and_29 (and_29_out, not_117_out, a1, not_118_out, not_119_out, a4, a6, not_120_out);
  and and_30 (and_30_out, not_121_out, a1, not_122_out, a3, a4, not_123_out, not_124_out, not_125_out);
  and and_31 (and_31_out, not_126_out, not_127_out, a2, a3, not_128_out, a5, not_129_out, not_130_out);
  and and_32 (and_32_out, not_131_out, a1, not_132_out, not_133_out, a4, not_134_out, a6);
  and and_33 (and_33_out, not_135_out, a1, not_136_out, a3, not_137_out, not_138_out, not_139_out, a7);
  and and_34 (and_34_out, not_140_out, a1, not_141_out, a3, not_142_out, a6, not_143_out);
  and and_35 (and_35_out, not_144_out, a1, not_145_out, a3, not_146_out, a5, a6);
  and and_36 (and_36_out, not_147_out, not_148_out, a2, a3, not_149_out, not_150_out);
  and and_37 (and_37_out, not_151_out, not_152_out, a2, a3, not_153_out, not_154_out, a6);
  and and_38 (and_38_out, not_155_out, not_156_out, a2, a3, not_157_out, a5, not_158_out);
  and and_39 (and_39_out, not_159_out, not_160_out, a2, a3, a4, not_161_out, not_162_out);
  and and_40 (and_40_out, not_163_out, a1, not_164_out, not_165_out, not_166_out, not_167_out, a6);
  and and_41 (and_41_out, not_168_out, a1, not_169_out, not_170_out, not_171_out, a6, a7);
  and and_42 (and_42_out, not_172_out, a1, not_173_out, not_174_out, a5, not_175_out, not_176_out);
  and and_43 (and_43_out, not_177_out, a1, not_178_out, not_179_out, not_180_out, a5, a7);
  and and_44 (and_44_out, not_181_out, a1, not_182_out, not_183_out, a5, a6, a7);
  and and_45 (and_45_out, not_184_out, a1, not_185_out, not_186_out, a4, not_187_out, not_188_out, a7);
  and and_46 (and_46_out, not_189_out, a1, not_190_out, a3, not_191_out, not_192_out, a7);
  and and_47 (and_47_out, not_193_out, a1, not_194_out, a3, a4, not_195_out, a6, not_196_out);
  or or_1 (x00, and_1_out, and_2_out, and_3_out, and_4_out, and_5_out, and_6_out, and_7_out, and_8_out, and_9_out, and_10_out, and_11_out);
  or or_2 (x10, and_12_out, and_13_out, and_14_out);
  or or_3 (x20, and_15_out, and_16_out, and_17_out, and_18_out);
  or or_4 (x30, and_19_out, and_20_out, and_21_out, and_22_out, and_23_out, and_24_out, and_25_out, and_26_out, and_27_out);
  or or_5 (x40, and_28_out, and_29_out, and_30_out);
  or or_6 (x50, and_31_out, and_32_out, and_33_out, and_34_out, and_35_out);
  or or_7 (x60, and_36_out, and_37_out, and_38_out, and_39_out, and_40_out, and_41_out, and_42_out, and_43_out, and_44_out, and_45_out, and_46_out, and_47_out);
endmodule

module COLUNA_4 (
  input  a0,
  input  a1,
  input  a2,
  input  a3,
  input  a4,
  input  a5,
  input  a6,
  input  a7,
  output x00,
  output x10,
  output x20,
  output x30,
  output x40,
  output x50,
  output x60
);

  wire and_1_out, and_2_out, and_3_out, and_4_out, and_5_out, and_6_out, and_7_out, and_8_out, and_9_out,
       and_10_out, and_11_out, and_12_out, and_13_out, and_14_out, and_15_out, and_16_out, and_17_out,
       and_18_out, and_19_out, and_20_out, and_21_out, and_22_out, and_23_out, and_24_out, and_25_out,
       and_26_out, and_27_out, and_28_out, and_29_out, and_30_out, and_31_out, and_32_out, and_33_out,
       and_34_out, and_35_out, and_36_out, and_37_out, and_38_out, and_39_out, and_40_out, and_41_out,
       and_42_out, and_43_out, and_44_out, and_45_out, and_46_out, and_47_out, and_48_out, and_49_out,
       and_50_out, and_51_out, and_52_out, and_53_out, and_54_out, and_55_out, and_56_out, and_57_out,
       and_58_out, and_59_out, and_60_out, and_61_out, and_62_out, and_63_out, and_64_out, and_65_out,
       and_66_out, and_67_out, and_68_out, and_69_out, and_70_out, and_71_out, and_72_out, and_73_out,
       and_74_out, and_75_out, and_76_out, and_77_out, and_78_out, and_79_out, not_1_out, not_2_out,
       not_3_out, not_4_out, not_5_out, not_6_out, not_7_out, not_8_out, not_9_out, not_10_out, not_11_out,
       not_12_out, not_13_out, not_14_out, not_15_out, not_16_out, not_17_out, not_18_out, not_19_out,
       not_20_out, not_21_out, not_22_out, not_23_out, not_24_out, not_25_out, not_26_out, not_27_out,
       not_28_out, not_29_out, not_30_out, not_31_out, not_32_out, not_33_out, not_34_out, not_35_out,
       not_36_out, not_37_out, not_38_out, not_39_out, not_40_out, not_41_out, not_42_out, not_43_out,
       not_44_out, not_45_out, not_46_out, not_47_out, not_48_out, not_49_out, not_50_out, not_51_out,
       not_52_out, not_53_out, not_54_out, not_55_out, not_56_out, not_57_out, not_58_out, not_59_out,
       not_60_out, not_61_out, not_62_out, not_63_out, not_64_out, not_65_out, not_66_out, not_67_out,
       not_68_out, not_69_out, not_70_out, not_71_out, not_72_out, not_73_out, not_74_out, not_75_out,
       not_76_out, not_77_out, not_78_out, not_79_out, not_80_out, not_81_out, not_82_out, not_83_out,
       not_84_out, not_85_out, not_86_out, not_87_out, not_88_out, not_89_out, not_90_out, not_91_out,
       not_92_out, not_93_out, not_94_out, not_95_out, not_96_out, not_97_out, not_98_out, not_99_out,
       not_100_out, not_101_out, not_102_out, not_103_out, not_104_out, not_105_out, not_106_out,
       not_107_out, not_108_out, not_109_out, not_110_out, not_111_out, not_112_out, not_113_out,
       not_114_out, not_115_out, not_116_out, not_117_out, not_118_out, not_119_out, not_120_out,
       not_121_out, not_122_out, not_123_out, not_124_out, not_125_out, not_126_out, not_127_out,
       not_128_out, not_129_out, not_130_out, not_131_out, not_132_out, not_133_out, not_134_out,
       not_135_out, not_136_out, not_137_out, not_138_out, not_139_out, not_140_out, not_141_out,
       not_142_out, not_143_out, not_144_out, not_145_out, not_146_out, not_147_out, not_148_out,
       not_149_out, not_150_out, not_151_out, not_152_out, not_153_out, not_154_out, not_155_out,
       not_156_out, not_157_out, not_158_out, not_159_out, not_160_out, not_161_out, not_162_out,
       not_163_out, not_164_out, not_165_out, not_166_out, not_167_out, not_168_out, not_169_out,
       not_170_out, not_171_out, not_172_out, not_173_out, not_174_out, not_175_out, not_176_out,
       not_177_out, not_178_out, not_179_out, not_180_out, not_181_out, not_182_out, not_183_out,
       not_184_out, not_185_out, not_186_out, not_187_out, not_188_out, not_189_out, not_190_out,
       not_191_out, not_192_out, not_193_out, not_194_out, not_195_out, not_196_out, not_197_out,
       not_198_out, not_199_out, not_200_out, not_201_out, not_202_out, not_203_out, not_204_out,
       not_205_out, not_206_out, not_207_out, not_208_out, not_209_out, not_210_out, not_211_out,
       not_212_out, not_213_out, not_214_out, not_215_out, not_216_out, not_217_out, not_218_out,
       not_219_out, not_220_out, not_221_out, not_222_out, not_223_out, not_224_out, not_225_out,
       not_226_out, not_227_out, not_228_out, not_229_out, not_230_out, not_231_out, not_232_out,
       not_233_out, not_234_out, not_235_out, not_236_out, not_237_out, not_238_out, not_239_out,
       not_240_out, not_241_out, not_242_out, not_243_out, not_244_out, not_245_out, not_246_out,
       not_247_out, not_248_out, not_249_out, not_250_out, not_251_out, not_252_out, not_253_out,
       not_254_out, not_255_out, not_256_out, not_257_out, not_258_out, not_259_out, not_260_out,
       not_261_out, not_262_out, not_263_out, not_264_out, not_265_out, not_266_out, not_267_out,
       not_268_out, not_269_out, not_270_out, not_271_out, not_272_out, not_273_out, not_274_out,
       not_275_out, not_276_out, not_277_out, not_278_out, not_279_out, not_280_out, not_281_out,
       not_282_out, not_283_out, not_284_out, not_285_out, not_286_out, not_287_out, not_288_out,
       not_289_out, not_290_out, not_291_out, not_292_out, not_293_out, not_294_out, not_295_out,
       not_296_out, not_297_out, not_298_out, not_299_out, not_300_out, not_301_out, not_302_out,
       not_303_out, not_304_out, not_305_out, not_306_out, not_307_out, not_308_out, not_309_out,
       not_310_out, not_311_out, not_312_out, not_313_out, not_314_out, not_315_out, not_316_out,
       not_317_out, not_318_out, not_319_out, not_320_out, not_321_out, not_322_out, not_323_out,
       not_324_out, not_325_out, not_326_out, not_327_out, not_328_out, not_329_out, not_330_out;

  not not_1 (not_1_out, a0);
  not not_2 (not_2_out, a1);
  not not_3 (not_3_out, a4);
  not not_4 (not_4_out, a0);
  not not_5 (not_5_out, a2);
  not not_6 (not_6_out, a3);
  not not_7 (not_7_out, a5);
  not not_8 (not_8_out, a0);
  not not_9 (not_9_out, a2);
  not not_10 (not_10_out, a4);
  not not_11 (not_11_out, a0);
  not not_12 (not_12_out, a2);
  not not_13 (not_13_out, a3);
  not not_14 (not_14_out, a6);
  not not_15 (not_15_out, a0);
  not not_16 (not_16_out, a2);
  not not_17 (not_17_out, a3);
  not not_18 (not_18_out, a7);
  not not_19 (not_19_out, a0);
  not not_20 (not_20_out, a2);
  not not_21 (not_21_out, a5);
  not not_22 (not_22_out, a6);
  not not_23 (not_23_out, a0);
  not not_24 (not_24_out, a2);
  not not_25 (not_25_out, a4);
  not not_26 (not_26_out, a0);
  not not_27 (not_27_out, a2);
  not not_28 (not_28_out, a5);
  not not_29 (not_29_out, a7);
  not not_30 (not_30_out, a0);
  not not_31 (not_31_out, a1);
  not not_32 (not_32_out, a4);
  not not_33 (not_33_out, a5);
  not not_34 (not_34_out, a7);
  not not_35 (not_35_out, a0);
  not not_36 (not_36_out, a1);
  not not_37 (not_37_out, a4);
  not not_38 (not_38_out, a0);
  not not_39 (not_39_out, a1);
  not not_40 (not_40_out, a5);
  not not_41 (not_41_out, a6);
  not not_42 (not_42_out, a0);
  not not_43 (not_43_out, a2);
  not not_44 (not_44_out, a4);
  not not_45 (not_45_out, a5);
  not not_46 (not_46_out, a6);
  not not_47 (not_47_out, a0);
  not not_48 (not_48_out, a2);
  not not_49 (not_49_out, a4);
  not not_50 (not_50_out, a5);
  not not_51 (not_51_out, a7);
  not not_52 (not_52_out, a0);
  not not_53 (not_53_out, a2);
  not not_54 (not_54_out, a3);
  not not_55 (not_55_out, a4);
  not not_56 (not_56_out, a6);
  not not_57 (not_57_out, a7);
  not not_58 (not_58_out, a0);
  not not_59 (not_59_out, a2);
  not not_60 (not_60_out, a5);
  not not_61 (not_61_out, a6);
  not not_62 (not_62_out, a7);
  not not_63 (not_63_out, a0);
  not not_64 (not_64_out, a2);
  not not_65 (not_65_out, a3);
  not not_66 (not_66_out, a0);
  not not_67 (not_67_out, a2);
  not not_68 (not_68_out, a3);
  not not_69 (not_69_out, a0);
  not not_70 (not_70_out, a2);
  not not_71 (not_71_out, a5);
  not not_72 (not_72_out, a6);
  not not_73 (not_73_out, a0);
  not not_74 (not_74_out, a2);
  not not_75 (not_75_out, a5);
  not not_76 (not_76_out, a7);
  not not_77 (not_77_out, a0);
  not not_78 (not_78_out, a2);
  not not_79 (not_79_out, a4);
  not not_80 (not_80_out, a0);
  not not_81 (not_81_out, a2);
  not not_82 (not_82_out, a4);
  not not_83 (not_83_out, a0);
  not not_84 (not_84_out, a1);
  not not_85 (not_85_out, a4);
  not not_86 (not_86_out, a5);
  not not_87 (not_87_out, a7);
  not not_88 (not_88_out, a0);
  not not_89 (not_89_out, a1);
  not not_90 (not_90_out, a4);
  not not_91 (not_91_out, a5);
  not not_92 (not_92_out, a0);
  not not_93 (not_93_out, a1);
  not not_94 (not_94_out, a5);
  not not_95 (not_95_out, a6);
  not not_96 (not_96_out, a0);
  not not_97 (not_97_out, a2);
  not not_98 (not_98_out, a4);
  not not_99 (not_99_out, a5);
  not not_100 (not_100_out, a6);
  not not_101 (not_101_out, a0);
  not not_102 (not_102_out, a2);
  not not_103 (not_103_out, a4);
  not not_104 (not_104_out, a5);
  not not_105 (not_105_out, a7);
  not not_106 (not_106_out, a0);
  not not_107 (not_107_out, a2);
  not not_108 (not_108_out, a3);
  not not_109 (not_109_out, a4);
  not not_110 (not_110_out, a6);
  not not_111 (not_111_out, a7);
  not not_112 (not_112_out, a0);
  not not_113 (not_113_out, a2);
  not not_114 (not_114_out, a3);
  not not_115 (not_115_out, a5);
  not not_116 (not_116_out, a6);
  not not_117 (not_117_out, a7);
  not not_118 (not_118_out, a0);
  not not_119 (not_119_out, a2);
  not not_120 (not_120_out, a3);
  not not_121 (not_121_out, a0);
  not not_122 (not_122_out, a2);
  not not_123 (not_123_out, a3);
  not not_124 (not_124_out, a0);
  not not_125 (not_125_out, a2);
  not not_126 (not_126_out, a4);
  not not_127 (not_127_out, a5);
  not not_128 (not_128_out, a6);
  not not_129 (not_129_out, a0);
  not not_130 (not_130_out, a2);
  not not_131 (not_131_out, a4);
  not not_132 (not_132_out, a6);
  not not_133 (not_133_out, a0);
  not not_134 (not_134_out, a2);
  not not_135 (not_135_out, a4);
  not not_136 (not_136_out, a0);
  not not_137 (not_137_out, a1);
  not not_138 (not_138_out, a4);
  not not_139 (not_139_out, a5);
  not not_140 (not_140_out, a6);
  not not_141 (not_141_out, a7);
  not not_142 (not_142_out, a0);
  not not_143 (not_143_out, a1);
  not not_144 (not_144_out, a4);
  not not_145 (not_145_out, a6);
  not not_146 (not_146_out, a0);
  not not_147 (not_147_out, a1);
  not not_148 (not_148_out, a5);
  not not_149 (not_149_out, a6);
  not not_150 (not_150_out, a0);
  not not_151 (not_151_out, a2);
  not not_152 (not_152_out, a4);
  not not_153 (not_153_out, a5);
  not not_154 (not_154_out, a6);
  not not_155 (not_155_out, a0);
  not not_156 (not_156_out, a2);
  not not_157 (not_157_out, a3);
  not not_158 (not_158_out, a4);
  not not_159 (not_159_out, a6);
  not not_160 (not_160_out, a7);
  not not_161 (not_161_out, a0);
  not not_162 (not_162_out, a2);
  not not_163 (not_163_out, a3);
  not not_164 (not_164_out, a0);
  not not_165 (not_165_out, a2);
  not not_166 (not_166_out, a3);
  not not_167 (not_167_out, a5);
  not not_168 (not_168_out, a6);
  not not_169 (not_169_out, a7);
  not not_170 (not_170_out, a0);
  not not_171 (not_171_out, a2);
  not not_172 (not_172_out, a3);
  not not_173 (not_173_out, a0);
  not not_174 (not_174_out, a2);
  not not_175 (not_175_out, a3);
  not not_176 (not_176_out, a0);
  not not_177 (not_177_out, a2);
  not not_178 (not_178_out, a4);
  not not_179 (not_179_out, a6);
  not not_180 (not_180_out, a0);
  not not_181 (not_181_out, a2);
  not not_182 (not_182_out, a4);
  not not_183 (not_183_out, a0);
  not not_184 (not_184_out, a1);
  not not_185 (not_185_out, a4);
  not not_186 (not_186_out, a6);
  not not_187 (not_187_out, a7);
  not not_188 (not_188_out, a0);
  not not_189 (not_189_out, a1);
  not not_190 (not_190_out, a4);
  not not_191 (not_191_out, a5);
  not not_192 (not_192_out, a0);
  not not_193 (not_193_out, a1);
  not not_194 (not_194_out, a4);
  not not_195 (not_195_out, a6);
  not not_196 (not_196_out, a0);
  not not_197 (not_197_out, a1);
  not not_198 (not_198_out, a4);
  not not_199 (not_199_out, a7);
  not not_200 (not_200_out, a0);
  not not_201 (not_201_out, a1);
  not not_202 (not_202_out, a5);
  not not_203 (not_203_out, a6);
  not not_204 (not_204_out, a0);
  not not_205 (not_205_out, a2);
  not not_206 (not_206_out, a4);
  not not_207 (not_207_out, a5);
  not not_208 (not_208_out, a6);
  not not_209 (not_209_out, a0);
  not not_210 (not_210_out, a2);
  not not_211 (not_211_out, a3);
  not not_212 (not_212_out, a4);
  not not_213 (not_213_out, a5);
  not not_214 (not_214_out, a7);
  not not_215 (not_215_out, a0);
  not not_216 (not_216_out, a2);
  not not_217 (not_217_out, a3);
  not not_218 (not_218_out, a4);
  not not_219 (not_219_out, a6);
  not not_220 (not_220_out, a7);
  not not_221 (not_221_out, a0);
  not not_222 (not_222_out, a2);
  not not_223 (not_223_out, a3);
  not not_224 (not_224_out, a0);
  not not_225 (not_225_out, a2);
  not not_226 (not_226_out, a3);
  not not_227 (not_227_out, a5);
  not not_228 (not_228_out, a6);
  not not_229 (not_229_out, a7);
  not not_230 (not_230_out, a0);
  not not_231 (not_231_out, a2);
  not not_232 (not_232_out, a3);
  not not_233 (not_233_out, a0);
  not not_234 (not_234_out, a2);
  not not_235 (not_235_out, a3);
  not not_236 (not_236_out, a0);
  not not_237 (not_237_out, a2);
  not not_238 (not_238_out, a4);
  not not_239 (not_239_out, a0);
  not not_240 (not_240_out, a2);
  not not_241 (not_241_out, a4);
  not not_242 (not_242_out, a0);
  not not_243 (not_243_out, a1);
  not not_244 (not_244_out, a5);
  not not_245 (not_245_out, a6);
  not not_246 (not_246_out, a7);
  not not_247 (not_247_out, a0);
  not not_248 (not_248_out, a1);
  not not_249 (not_249_out, a4);
  not not_250 (not_250_out, a5);
  not not_251 (not_251_out, a0);
  not not_252 (not_252_out, a1);
  not not_253 (not_253_out, a4);
  not not_254 (not_254_out, a6);
  not not_255 (not_255_out, a0);
  not not_256 (not_256_out, a1);
  not not_257 (not_257_out, a4);
  not not_258 (not_258_out, a7);
  not not_259 (not_259_out, a0);
  not not_260 (not_260_out, a1);
  not not_261 (not_261_out, a5);
  not not_262 (not_262_out, a6);
  not not_263 (not_263_out, a0);
  not not_264 (not_264_out, a2);
  not not_265 (not_265_out, a4);
  not not_266 (not_266_out, a5);
  not not_267 (not_267_out, a6);
  not not_268 (not_268_out, a0);
  not not_269 (not_269_out, a2);
  not not_270 (not_270_out, a3);
  not not_271 (not_271_out, a4);
  not not_272 (not_272_out, a5);
  not not_273 (not_273_out, a7);
  not not_274 (not_274_out, a0);
  not not_275 (not_275_out, a2);
  not not_276 (not_276_out, a3);
  not not_277 (not_277_out, a4);
  not not_278 (not_278_out, a6);
  not not_279 (not_279_out, a7);
  not not_280 (not_280_out, a0);
  not not_281 (not_281_out, a2);
  not not_282 (not_282_out, a4);
  not not_283 (not_283_out, a0);
  not not_284 (not_284_out, a2);
  not not_285 (not_285_out, a5);
  not not_286 (not_286_out, a6);
  not not_287 (not_287_out, a7);
  not not_288 (not_288_out, a0);
  not not_289 (not_289_out, a2);
  not not_290 (not_290_out, a3);
  not not_291 (not_291_out, a0);
  not not_292 (not_292_out, a2);
  not not_293 (not_293_out, a3);
  not not_294 (not_294_out, a0);
  not not_295 (not_295_out, a2);
  not not_296 (not_296_out, a4);
  not not_297 (not_297_out, a0);
  not not_298 (not_298_out, a1);
  not not_299 (not_299_out, a4);
  not not_300 (not_300_out, a5);
  not not_301 (not_301_out, a7);
  not not_302 (not_302_out, a0);
  not not_303 (not_303_out, a2);
  not not_304 (not_304_out, a3);
  not not_305 (not_305_out, a5);
  not not_306 (not_306_out, a0);
  not not_307 (not_307_out, a2);
  not not_308 (not_308_out, a3);
  not not_309 (not_309_out, a6);
  not not_310 (not_310_out, a0);
  not not_311 (not_311_out, a2);
  not not_312 (not_312_out, a4);
  not not_313 (not_313_out, a5);
  not not_314 (not_314_out, a6);
  not not_315 (not_315_out, a0);
  not not_316 (not_316_out, a2);
  not not_317 (not_317_out, a5);
  not not_318 (not_318_out, a6);
  not not_319 (not_319_out, a7);
  not not_320 (not_320_out, a0);
  not not_321 (not_321_out, a2);
  not not_322 (not_322_out, a3);
  not not_323 (not_323_out, a7);
  not not_324 (not_324_out, a0);
  not not_325 (not_325_out, a2);
  not not_326 (not_326_out, a5);
  not not_327 (not_327_out, a7);
  not not_328 (not_328_out, a0);
  not not_329 (not_329_out, a2);
  not not_330 (not_330_out, a4);
  and and_1 (and_1_out, not_1_out, not_2_out, a2, a3, not_3_out, a5, a7);
  and and_2 (and_2_out, not_4_out, a1, not_5_out, not_6_out, not_7_out, a6, a7);
  and and_3 (and_3_out, not_8_out, a1, not_9_out, not_10_out, a6, a7);
  and and_4 (and_4_out, not_11_out, a1, not_12_out, not_13_out, a5, not_14_out, a7);
  and and_5 (and_5_out, not_15_out, a1, not_16_out, not_17_out, a5, a6, not_18_out);
  and and_6 (and_6_out, not_19_out, a1, not_20_out, a4, not_21_out, not_22_out);
  and and_7 (and_7_out, not_23_out, a1, not_24_out, a3, not_25_out, a5);
  and and_8 (and_8_out, not_26_out, a1, not_27_out, a3, a4, not_28_out, not_29_out);
  and and_9 (and_9_out, not_30_out, not_31_out, a2, a3, not_32_out, not_33_out, not_34_out);
  and and_10 (and_10_out, not_35_out, not_36_out, a2, a3, not_37_out, a6);
  and and_11 (and_11_out, not_38_out, not_39_out, a2, a3, a4, not_40_out, not_41_out);
  and and_12 (and_12_out, not_42_out, a1, not_43_out, not_44_out, not_45_out, not_46_out, a7);
  and and_13 (and_13_out, not_47_out, a1, not_48_out, not_49_out, not_50_out, a6, not_51_out);
  and and_14 (and_14_out, not_52_out, a1, not_53_out, not_54_out, not_55_out, a5, not_56_out, not_57_out);
  and and_15 (and_15_out, not_58_out, a1, not_59_out, a4, not_60_out, not_61_out, not_62_out);
  and and_16 (and_16_out, not_63_out, a1, not_64_out, not_65_out, a4, a5, a7);
  and and_17 (and_17_out, not_66_out, a1, not_67_out, not_68_out, a4, a5, a6);
  and and_18 (and_18_out, not_69_out, a1, not_70_out, a3, not_71_out, not_72_out);
  and and_19 (and_19_out, not_73_out, a1, not_74_out, a3, not_75_out, not_76_out);
  and and_20 (and_20_out, not_77_out, a1, not_78_out, a3, not_79_out, a5, a7);
  and and_21 (and_21_out, not_80_out, a1, not_81_out, a3, not_82_out, a5, a6);
  and and_22 (and_22_out, not_83_out, not_84_out, a2, a3, not_85_out, not_86_out, not_87_out);
  and and_23 (and_23_out, not_88_out, not_89_out, a2, a3, not_90_out, not_91_out, a6);
  and and_24 (and_24_out, not_92_out, not_93_out, a2, a3, a4, not_94_out, not_95_out);
  and and_25 (and_25_out, not_96_out, a1, not_97_out, not_98_out, not_99_out, not_100_out, a7);
  and and_26 (and_26_out, not_101_out, a1, not_102_out, not_103_out, not_104_out, a6, not_105_out);
  and and_27 (and_27_out, not_106_out, a1, not_107_out, not_108_out, not_109_out, a5, not_110_out, not_111_out);
  and and_28 (and_28_out, not_112_out, a1, not_113_out, not_114_out, a4, not_115_out, not_116_out, not_117_out);
  and and_29 (and_29_out, not_118_out, a1, not_119_out, not_120_out, a4, a5, a7);
  and and_30 (and_30_out, not_121_out, a1, not_122_out, not_123_out, a4, a5, a6);
  and and_31 (and_31_out, not_124_out, a1, not_125_out, a3, not_126_out, not_127_out, not_128_out);
  and and_32 (and_32_out, not_129_out, a1, not_130_out, a3, not_131_out, not_132_out, a7);
  and and_33 (and_33_out, not_133_out, a1, not_134_out, a3, not_135_out, a5, a6);
  and and_34 (and_34_out, not_136_out, not_137_out, a2, a3, not_138_out, not_139_out, not_140_out, not_141_out);
  and and_35 (and_35_out, not_142_out, not_143_out, a2, a3, not_144_out, a5, not_145_out, a7);
  and and_36 (and_36_out, not_146_out, not_147_out, a2, a3, a4, not_148_out, not_149_out, a7);
  and and_37 (and_37_out, not_150_out, a1, not_151_out, not_152_out, not_153_out, not_154_out, a7);
  and and_38 (and_38_out, not_155_out, a1, not_156_out, not_157_out, not_158_out, a5, not_159_out, not_160_out);
  and and_39 (and_39_out, not_161_out, a1, not_162_out, not_163_out, a5, a6, a7);
  and and_40 (and_40_out, not_164_out, a1, not_165_out, not_166_out, a4, not_167_out, not_168_out, not_169_out);
  and and_41 (and_41_out, not_170_out, a1, not_171_out, not_172_out, a4, a5, a7);
  and and_42 (and_42_out, not_173_out, a1, not_174_out, not_175_out, a4, a5, a6);
  and and_43 (and_43_out, not_176_out, a1, not_177_out, a3, not_178_out, not_179_out, a7);
  and and_44 (and_44_out, not_180_out, a1, not_181_out, a3, not_182_out, a5, a6);
  and and_45 (and_45_out, not_183_out, not_184_out, a2, a3, not_185_out, not_186_out, not_187_out);
  and and_46 (and_46_out, not_188_out, not_189_out, a2, a3, not_190_out, not_191_out, a6, a7);
  and and_47 (and_47_out, not_192_out, not_193_out, a2, a3, not_194_out, a5, not_195_out);
  and and_48 (and_48_out, not_196_out, not_197_out, a2, a3, not_198_out, a5, not_199_out);
  and and_49 (and_49_out, not_200_out, not_201_out, a2, a3, a4, not_202_out, not_203_out);
  and and_50 (and_50_out, not_204_out, a1, not_205_out, not_206_out, not_207_out, not_208_out, a7);
  and and_51 (and_51_out, not_209_out, a1, not_210_out, not_211_out, not_212_out, not_213_out, a6, not_214_out);
  and and_52 (and_52_out, not_215_out, a1, not_216_out, not_217_out, not_218_out, a5, not_219_out, not_220_out);
  and and_53 (and_53_out, not_221_out, a1, not_222_out, not_223_out, a5, a6, a7);
  and and_54 (and_54_out, not_224_out, a1, not_225_out, not_226_out, a4, not_227_out, not_228_out, not_229_out);
  and and_55 (and_55_out, not_230_out, a1, not_231_out, not_232_out, a4, a5, a7);
  and and_56 (and_56_out, not_233_out, a1, not_234_out, not_235_out, a4, a5, a6);
  and and_57 (and_57_out, not_236_out, a1, not_237_out, a3, not_238_out, a7);
  and and_58 (and_58_out, not_239_out, a1, not_240_out, a3, not_241_out, a5, a6);
  and and_59 (and_59_out, not_242_out, not_243_out, a2, a3, not_244_out, not_245_out, not_246_out);
  and and_60 (and_60_out, not_247_out, not_248_out, a2, a3, not_249_out, not_250_out, a6, a7);
  and and_61 (and_61_out, not_251_out, not_252_out, a2, a3, not_253_out, a5, not_254_out, a7);
  and and_62 (and_62_out, not_255_out, not_256_out, a2, a3, not_257_out, a5, a6, not_258_out);
  and and_63 (and_63_out, not_259_out, not_260_out, a2, a3, a4, not_261_out, not_262_out);
  and and_64 (and_64_out, not_263_out, a1, not_264_out, not_265_out, not_266_out, not_267_out, a7);
  and and_65 (and_65_out, not_268_out, a1, not_269_out, not_270_out, not_271_out, not_272_out, a6, not_273_out);
  and and_66 (and_66_out, not_274_out, a1, not_275_out, not_276_out, not_277_out, a5, not_278_out, not_279_out);
  and and_67 (and_67_out, not_280_out, a1, not_281_out, not_282_out, a5, a6, a7);
  and and_68 (and_68_out, not_283_out, a1, not_284_out, a4, not_285_out, not_286_out, not_287_out);
  and and_69 (and_69_out, not_288_out, a1, not_289_out, not_290_out, a4, a5, a7);
  and and_70 (and_70_out, not_291_out, a1, not_292_out, not_293_out, a4, a5, a6);
  and and_71 (and_71_out, not_294_out, a1, not_295_out, a3, not_296_out, a7);
  and and_72 (and_72_out, not_297_out, not_298_out, a2, a3, not_299_out, not_300_out, a6, not_301_out);
  and and_73 (and_73_out, not_302_out, a1, not_303_out, not_304_out, not_305_out, a7);
  and and_74 (and_74_out, not_306_out, a1, not_307_out, not_308_out, not_309_out, a7);
  and and_75 (and_75_out, not_310_out, a1, not_311_out, not_312_out, not_313_out, not_314_out, a7);
  and and_76 (and_76_out, not_315_out, a1, not_316_out, a4, not_317_out, not_318_out, not_319_out);
  and and_77 (and_77_out, not_320_out, a1, not_321_out, not_322_out, a4, a5, not_323_out);
  and and_78 (and_78_out, not_324_out, a1, not_325_out, a3, not_326_out, a6, not_327_out);
  and and_79 (and_79_out, not_328_out, a1, not_329_out, a3, not_330_out, a5, a6, a7);
  or or_1 (x00, and_1_out, and_2_out, and_3_out, and_4_out, and_5_out, and_6_out, and_7_out, and_8_out);
  or or_2 (x10, and_9_out, and_10_out, and_11_out, and_12_out, and_13_out, and_14_out, and_15_out, and_16_out, and_17_out, and_18_out, and_19_out, and_20_out, and_21_out);
  or or_3 (x20, and_22_out, and_23_out, and_24_out, and_25_out, and_26_out, and_27_out, and_28_out, and_29_out, and_30_out, and_31_out, and_32_out, and_33_out);
  or or_4 (x30, and_34_out, and_35_out, and_36_out, and_37_out, and_38_out, and_39_out, and_40_out, and_41_out, and_42_out, and_43_out, and_44_out);
  or or_5 (x40, and_45_out, and_46_out, and_47_out, and_48_out, and_49_out, and_50_out, and_51_out, and_52_out, and_53_out, and_54_out, and_55_out, and_56_out, and_57_out, and_58_out);
  or or_6 (x50, and_59_out, and_60_out, and_61_out, and_62_out, and_63_out, and_64_out, and_65_out, and_66_out, and_67_out, and_68_out, and_69_out, and_70_out, and_71_out);
  or or_7 (x60, and_72_out, and_73_out, and_74_out, and_75_out, and_76_out, and_77_out, and_78_out, and_79_out);
endmodule

module NUMERO_TO_ASCII (
  input  [3:0] in_1,
  output [7:0] out_2
);


  assign out_2 = {4'b0011, in_1};
endmodule
